// Logisim project BARREDORA.circ as structural Verilog: 4 circuits, main circuit main
module main (
  input  B,
  input  RST,
  output out_3,
  output out_4
);

  wire CLK_out, logicaedosig_1_d0, logicaedosig_1_d1, memorias_1_q0, memorias_1_q1;

  LogicaEdoSig logicaedosig_1 (
    .Q1(memorias_1_q1), .Q0(memorias_1_q0), .B(B), .D1(logicaedosig_1_d1), .D0(logicaedosig_1_d0));
  Clock CLK (.out(CLK_out));
  Memorias memorias_1 (
    .D1(logicaedosig_1_d1), .D0(logicaedosig_1_d0), .CLK(CLK_out), .RST(RST), .Q1(memorias_1_q1),
    .Q0(memorias_1_q0));
  LogicaSalidas logicasalidas_1 (.Q1(memorias_1_q1), .Q0(memorias_1_q0), .B(B), .RI(out_3), .RD(out_4));
endmodule

module LogicaEdoSig (
  input  Q1,
  input  Q0,
  input  B,
  output D1,
  output D0
);

  wire and_1_out, and_2_out, and_3_out, not_1_out, not_2_out, not_3_out;

  not not_1 (not_1_out, Q1);
  not not_2 (not_2_out, Q0);
  not not_3 (not_3_out, B);
  and and_1 (and_1_out, not_1_out, Q0, not_3_out);
  and and_2 (and_2_out, Q1, not_2_out);
  and and_3 (and_3_out, Q1, B);
  or or_1 (D1, and_1_out, and_2_out, and_3_out);

  assign D0 = B;
endmodule

module LogicaSalidas (
  input  Q1,
  input  Q0,
  input  B,
  output RI,
  output RD
);

  wire not_1_out, not_2_out;

  not not_1 (not_1_out, Q1);
  not not_2 (not_2_out, Q0);
  or or_1 (RI, not_2_out, Q1);
  or or_2 (RD, not_1_out, not_2_out);
endmodule

module Memorias (
  input  D1,
  input  D0,
  input  CLK,
  input  RST,
  output Q1,
  output Q0
);

  D_Flip_Flop d_ff_1 (.D(D1), .clk(CLK), .Q(Q1), .preset(1'b0), .reset(RST));  // open: Qn
  D_Flip_Flop d_ff_2 (.D(D0), .clk(CLK), .Q(Q0), .preset(1'b0), .reset(RST));  // open: Qn
endmodule
