// Logisim project FLIP_FLOPS.circ as structural Verilog: 1 circuit, main circuit main
module main (
  input  SEL,
  input  D,
  input  CLK,
  input  RST,
  input  in_5,
  input  in_6,
  output Q,
  output QN,
  output Q_JK,
  output QN_JK
);

  D_Flip_Flop d_ff_1 (.D(D), .clk(CLK), .Q(Q), .Qn(QN), .preset(SEL), .reset(RST));
  J_K_Flip_Flop j_k_ff_1 (.J(in_5), .K(in_6), .clk(CLK), .Q(Q_JK), .Qn(QN_JK), .preset(SEL), .reset(RST));
endmodule
