// Logisim project LS_PARIDAD.circ as structural Verilog: 4 circuits, main circuit main
module main (
  input  in_1,
  input  in_2,
  input  in_3,
  output out_4
);

  wire clock_1_out, logicaestadosig_1_j, logicaestadosig_1_k, memoria_1_q;

  logicaEstadoSig logicaestadosig_1 (.DIGITO(in_2), .J(logicaestadosig_1_j), .K(logicaestadosig_1_k));
  Clock clock_1 (.out(clock_1_out));
  MEMORIA memoria_1 (
    .S(in_1), .J(logicaestadosig_1_j), .K(logicaestadosig_1_k), .CLK(clock_1_out), .RST(in_3), .Q(memoria_1_q));
  logicaSalida logicasalida_1 (.q0(memoria_1_q), .digito(in_2), .par(out_4));
endmodule

module logicaSalida (
  input  q0,
  input  digito,
  output par
);

  not not_1 (par, q0);
endmodule

module logicaEstadoSig (
  input  DIGITO,
  output J,
  output K
);


  assign J = DIGITO;
  assign K = DIGITO;
endmodule

module MEMORIA (
  input  S,
  input  J,
  input  K,
  input  CLK,
  input  RST,
  output Q
);

  J_K_Flip_Flop j_k_ff_1 (.J(J), .K(K), .clk(CLK), .Q(Q), .preset(S), .reset(RST));  // open: Qn
endmodule
