// Logisim project MODULOS_ABCD.circ as structural Verilog: 1 circuit, main circuit main
module main (
  input  CLK,
  input  [3:0] REGISTROS,
  input  [2:0] BUFFERS,
  input  RST,
  input  [7:0] E,
  output [7:0] S
);

  wire [7:0] A_q, B_q, BUS_1, C_q;

  Register A (.D(E), .en(REGISTROS[0]), .clk(CLK), .Q(A_q), .clr(RST));
  Register B (.D(BUS_1), .en(REGISTROS[1]), .clk(CLK), .Q(B_q), .clr(RST));
  Register C (.D(BUS_1), .en(REGISTROS[2]), .clk(CLK), .Q(C_q), .clr(RST));
  assign BUS_1 = BUFFERS[0] ? A_q : 8'bz;  // Controlled_Buffer controlled_buffer_1
  assign BUS_1 = BUFFERS[1] ? B_q : 8'bz;  // Controlled_Buffer controlled_buffer_2
  assign BUS_1 = BUFFERS[2] ? C_q : 8'bz;  // Controlled_Buffer controlled_buffer_3
  Register D (.D(BUS_1), .en(REGISTROS[3]), .clk(CLK), .Q(S), .clr(RST));

  // Other names for the same wires on the sheet: BA = BUFFERS[0]; BB = BUFFERS[1]; BC = BUFFERS[2];
  //   WEA = REGISTROS[0]; WEB = REGISTROS[1]; WEC = REGISTROS[2]; WED = REGISTROS[3]
endmodule
