// Logisim project maquinamicro_bloquesDataPath.circ as structural Verilog
module main (
  input  reset,
  output out_2
);

  wire adder_1_cout, adder_2_cout, Clear, Clearr, clk, control_1_cs, control_1_oe, cs, demultiplexer_1_out0,
       demultiplexer_1_out1, demultiplexer_1_out2, demultiplexer_1_out3, demultiplexer_1_out4,
       demultiplexer_1_out5, demultiplexer_1_out6, demultiplexer_1_out7, inicia, Ipc, LF, Lf_t, LH, LL, Lpc,
       Lri, oe, SalAlu, SelDir, subtractor_1_bout, subtractor_2_bout, we, wr;
  wire [1:0] SalidaFlags;
  wire [2:0] ope, SelRegRA, SelRegRB, SelRegW;
  wire [4:0] control_1_idestado;
  wire [7:0] adder_1_out, adder_2_out, and_1_out, BusDatos, CO, Flags, not_1_out, register_5_q, register_6_q,
       register_7_q, register_8_q, register_9_q, register_10_q, register_11_q, register_12_q, SalA, SalB,
       SalidaALU, subtractor_1_out, subtractor_2_out;
  wire [15:0] dir, EntradaPC, salidaPC;

  Demultiplexer #(.select(3)) demultiplexer_1 (
    .out0(demultiplexer_1_out0), .out1(demultiplexer_1_out1), .out2(demultiplexer_1_out2),
    .out3(demultiplexer_1_out3), .out4(demultiplexer_1_out4), .out5(demultiplexer_1_out5),
    .out6(demultiplexer_1_out6), .out7(demultiplexer_1_out7), .in(wr), .sel(SelRegW));
  Register register_1 (.D(BusDatos), .en(Lri), .Q(CO), .clk(clk), .clr(Clear));
  Register register_2 (.D(BusDatos), .en(LH), .Q(EntradaPC[15:8]), .clk(clk), .clr(Clear));
  Multiplexer #(.width(16)) multiplexer_1 (.in0(salidaPC), .in1(EntradaPC), .out(dir), .sel(SelDir));
  assign and_1_out = SalA & SalB;  // AND_Gate and_1, 8 bits wide
  assign not_1_out = ~SalA;  // NOT_Gate not_1, 8 bits wide
  Subtractor subtractor_1 (.a(SalA), .b(8'h1), .out(subtractor_1_out), .bin(1'b0), .bout(subtractor_1_bout));
  Adder adder_1 (.a(SalA), .b(SalB), .out(adder_1_out), .cin(1'b0), .cout(adder_1_cout));
  Subtractor subtractor_2 (.a(SalA), .b(SalB), .out(subtractor_2_out), .bin(1'b0), .bout(subtractor_2_bout));
  Adder adder_2 (.a(SalA), .b(8'h1), .out(adder_2_out), .cin(1'b0), .cout(adder_2_cout));
  Register register_3 (.D({{5{1'b0}}, SalidaALU[7], SalidaFlags}), .en(Lf_t), .Q(Flags), .clk(clk), .clr(Clear));
  assign BusDatos = SalAlu ? SalidaALU : 8'bz;  // Controlled_Buffer controlled_buffer_1
  Counter #(.max('hffff), .width(16)) counter_1 (
    .load(Lpc), .D(EntradaPC), .count(Ipc), .Q(salidaPC), .up(1'b1), .clk(clk), .clr(Clear));  // open: carry
  Register register_4 (.D(BusDatos), .en(LL), .Q(EntradaPC[7:0]), .clk(clk), .clr(Clear));
  Register register_5 (.D(BusDatos), .en(demultiplexer_1_out0), .Q(register_5_q), .clk(clk), .clr(Clearr));
  Register register_6 (.D(BusDatos), .en(demultiplexer_1_out1), .Q(register_6_q), .clk(clk), .clr(Clearr));
  Register register_7 (.D(BusDatos), .en(demultiplexer_1_out2), .Q(register_7_q), .clk(clk), .clr(Clearr));
  Register register_8 (.D(BusDatos), .en(demultiplexer_1_out3), .Q(register_8_q), .clk(clk), .clr(Clearr));
  Register register_9 (.en(demultiplexer_1_out4), .Q(register_9_q), .clk(clk), .clr(Clearr));  // open: D
  Register register_10 (.D(BusDatos), .en(demultiplexer_1_out5), .Q(register_10_q), .clk(clk), .clr(Clearr));
  Register register_11 (.D(BusDatos), .en(demultiplexer_1_out6), .Q(register_11_q), .clk(clk), .clr(Clearr));
  Register register_12 (.D(BusDatos), .en(demultiplexer_1_out7), .Q(register_12_q), .clk(clk), .clr(Clearr));
  Clock clock_1 (.out(clk));
  Multiplexer #(.select(3), .width(8)) multiplexer_2 (
    .in0(register_5_q), .in1(register_6_q), .in2(register_7_q), .in3(register_8_q), .in4(register_9_q),
    .in5(register_10_q), .in6(register_11_q), .in7(register_12_q), .out(SalA), .sel(SelRegRA));
  Multiplexer #(.select(3), .width(8)) multiplexer_3 (
    .in0(register_5_q), .in1(register_6_q), .in2(register_7_q), .in3(register_8_q), .in4(register_9_q),
    .in5(register_10_q), .in6(register_11_q), .in7(register_12_q), .out(SalB), .sel(SelRegRB));
  Multiplexer #(.select(3), .width(8)) multiplexer_4 (
    .in0(SalA), .in1(SalB), .in2(and_1_out), .in3(not_1_out), .in4(subtractor_1_out), .in5(adder_1_out),
    .in6(subtractor_2_out), .in7(adder_2_out), .out(SalidaALU), .sel(ope));
  Comparator comparator_1 (.a(SalidaALU), .b({8{1'b0}}), .eq(SalidaFlags[0]));  // open: gt, lt
  Multiplexer #(.select(3)) multiplexer_5 (
    .in0(1'b0), .in1(1'b0), .in2(1'b0), .in3(1'b0), .in4(subtractor_1_bout), .in5(adder_1_cout),
    .in6(subtractor_2_bout), .in7(adder_2_cout), .out(SalidaFlags[1]), .sel(ope));
  RAM #(.asyncread("true"), .databus("bidir")) ram_1 (.addr(dir[7:0]), .we(we), .oe(oe), .clk(clk), .data(BusDatos));
  // Probe on dir[7:0]
  // Probe on BusDatos
  control control_1 (
    .clk(clk), .rst(reset), .Flags(Flags), .CO(CO), .clear(Clear), .Lpc(Lpc), .Ipc(Ipc), .SelDir(SelDir),
    .inicia(inicia), .cs(control_1_cs), .oe(control_1_oe), .we(we), .LH(LH), .LL(LL), .Lri(Lri),
    .SelRegW(SelRegW), .SelRegRA(SelRegRA), .SelRegRB(SelRegRB), .wr(wr), .ope(ope), .SalAlu(SalAlu),
    .LF(LF), .fin(out_2), .idEstado(control_1_idestado));
  not not_2 (cs, control_1_cs);
  not not_3 (oe, control_1_oe);
  // Probe on control_1_idestado

  // Other names for the same wires on the sheet: dirL[7:0] = dir[7:0]; dirH[7:0] = dir[15:8]; entDat[7:0] = BusDatos;
  //   SalidaFlags[2] = SalidaALU[7]; SalidaHL[15:0] = EntradaPC

  // Notes on the sheet:
  //   muxpchl
  //   flags
  //   ri
  //   pc
  //   hl
  //   bufferalu
  //   br
  //   alu
  //   FZ
  //   FS
  //   FC
  //   ram
endmodule

// VHDL entity memoria, as the project stores it:
library ieee;
use ieee.std_logic_1164.all;
use ieee.numeric_std.all;

entity memoria is
  generic (
    N: integer := 8;
    n_dir: integer := 8
  );
  port (
    clk: in std_logic;
    we: in std_logic;
    cs: in std_logic;
    oe: in std_logic;
    inicia: in std_logic;
--    dir: in std_logic_vector (n_dir -1 downto 0);
--    datos : inout std_logic_vector (N - 1 downto 0)
    dir: in std_logic_vector (7 downto 0);
    datos : inout std_logic_vector (7 downto 0)
  );
end entity memoria;

architecture Comportamiento of memoria is
  subtype registro is std_logic_vector (N - 1 downto 0);
  type banco is array (0 to (2 ** n_dir) - 1) of registro;
  
  function inicia_ram return banco is 
    variable tempo : banco := (others => (others => '0'));
  begin 
    for addr in 0 to 2 ** n_dir - 1 loop 
      -- Inicializa cada celda con el valor de su direccion
      tempo(addr) := std_logic_vector(to_unsigned(addr, N));
    end loop;
    -- Cambia las celdas donde esta el programa
    tempo(0) := x"70";  -- R1 <- M[0035]
    tempo(1) := x"35";
    tempo(2) := x"00";

    tempo(3) := x"46";  -- R0 <- R1

    tempo(4) := x"70";  -- R1 <- M[0036]
    tempo(5) := x"36";
    tempo(6) := x"00";

    tempo(7) := x"45";  -- R1 <- R0 + R1

    tempo(8) := x"71";  -- M[0037] <- R1
    tempo(9) := x"37";
    tempo(10) := x"00";
    
    tempo(11) := x"70";  -- R1 <- M[0037]
    tempo(12) := x"37";
    tempo(13) := x"00";
    
    tempo(14) := x"90";  -- No Existe   

    tempo(15) := x"FF";  -- Fin

    tempo(16#035#) := x"A4";
    tempo(16#036#) := x"B5";
    tempo(16#037#) := x"C6";
    
    return tempo;
  end inicia_ram;

  function inicia_ram2 return banco is 
    variable tempo : banco := (others => (others => '0'));
  begin 
    for addr in 0 to 2 ** n_dir - 1 loop 
      -- Inicializa cada celda con el valor de su direccion
      tempo(addr) := std_logic_vector(to_unsigned(addr, N));
    end loop;
    -- Cambia las celdas donde esta el programa
    tempo(0) := x"70";  -- R1 <- M[0035]
    tempo(1) := x"35";
    tempo(2) := x"00";

    tempo(3) := x"46";  -- R0 <- R1

    tempo(4) := x"47";  -- R1 <- 5E
    tempo(5) := x"5E";  
  
    tempo(6) := x"45";  -- R1 <- R0 + R1
    
    tempo(7) := x"71";  -- M[0036] <- R1
    tempo(8) := x"36";
    tempo(9) := x"00";

    tempo(10) := x"82";  -- JC 000F (15)
    tempo(11) := x"0F";
    tempo(12) := x"00";
    
    tempo(13) := x"10";
    tempo(14) := x"20";

    tempo(15) := x"42";  -- R1 <- R1 - 1

    tempo(16) := x"81";  -- JZ 002C (44)
    tempo(17) := x"2C";
    tempo(18) := x"00";
    
    tempo(19) := x"42";  -- R1 <- R1 - 1

    tempo(20) := x"81";  -- JZ 002C (25)
    tempo(21) := x"19";
    tempo(22) := x"00";
    
    tempo(23) := x"11";
    tempo(24) := x"21";
    
    tempo(25) := x"43";  -- R1 <- R1 + 1

    tempo(26) := x"40";  -- R1 <- not R1
    
    tempo(27) := x"83";  -- JS 0020 (32)
    tempo(28) := x"20";
    tempo(29) := x"00";
    
    tempo(30) := x"12";
    tempo(31) := x"22";
    
    tempo(32) := x"47";  -- R1 <- F9
    tempo(33) := x"F9";
    
    tempo(34) := x"41";  -- R1 <- R0 and R1
        
    tempo(35) := x"70";  -- R1 <- M[0036]
    tempo(36) := x"36";
    tempo(37) := x"00";

    tempo(38) := x"80";  -- JMP 002C (45)
    tempo(39) := x"2C";
    tempo(40) := x"00";
    
    tempo(41) := x"13";
    tempo(42) := x"14";
    tempo(43) := x"15";

    tempo(44) := x"FF";  -- Fin

    tempo(16#035#) := x"A4";
    tempo(16#036#) := x"B5";
    tempo(16#037#) := x"C6";
    
    return tempo;
  end inicia_ram2;

  function inicia_ram3 return banco is 
    variable tempo : banco := (others => (others => '0'));
  begin 
    for addr in 0 to 2 ** n_dir - 1 loop 
      -- Inicializa cada celda con el valor de su direccion
      tempo(addr) := std_logic_vector(to_unsigned(addr, N));
    end loop;
    -- Cambia las celdas donde esta el programa
    tempo(0) := x"47";  -- R1 <- 39
    tempo(1) := x"39";
    tempo(2) := x"46";  -- R0 <- R1
    tempo(3) := x"47";  -- R1 <- F3
    tempo(4) := x"F3";
    tempo(5) := x"45";  -- R1 <- R0 + R1
    tempo(6) := x"FF";  -- Fin

    return tempo;
  end inicia_ram3;

  function inicia_ram4 return banco is 
    variable tempo : banco := (others => (others => '0'));
  begin 
    for addr in 0 to 2 ** n_dir - 1 loop 
      -- Inicializa cada celda con el valor de su direccion
      tempo(addr) := std_logic_vector(to_unsigned(addr, N));
    end loop;
    -- Cambia las celdas donde esta el programa
    tempo(0) := x"47";  -- R1 <- 39
    tempo(1) := x"F3";
    tempo(2) := x"71";  -- M[0035] <- R1
    tempo(3) := x"35";  
    tempo(4) := x"00";
    tempo(5) := x"46";  -- R0 <- R1
    tempo(6) := x"47";  -- R1 <- F3
    tempo(7) := x"39";
    tempo(8) := x"71";  -- M[0036] <- R1
    tempo(9) := x"36";
    tempo(10) := x"00";
    tempo(11) := x"44";  -- R1 <- R0 - R1
    tempo(12) := x"82";  -- JC 0013 (19)
    tempo(13) := x"13";
    tempo(14) := x"00";
    tempo(15) := x"70";  -- R1 <- M[0035]
    tempo(16) := x"35";
    tempo(17) := x"00";
    tempo(18) := x"FF";  -- Fin
    tempo(19) := x"70";  -- R1 <- M[0036]
    tempo(20) := x"36";
    tempo(21) := x"00";
    tempo(22) := x"FF";  -- Fin

    return tempo;
  end inicia_ram4;

  function inicia_ram5 return banco is 
    variable tempo : banco := (others => (others => '0'));
  begin 
    for addr in 0 to 2 ** n_dir - 1 loop 
      -- Inicializa cada celda con el valor de su direccion
      tempo(addr) := std_logic_vector(to_unsigned(addr, N));
    end loop;
    -- Cambia las celdas donde esta el programa
    tempo(0) := x"70";  -- R1 <- M[0035]
    tempo(1) := x"35";
    tempo(2) := x"00";

    tempo(3) := x"46";  -- R0 <- R1

    tempo(4) := x"70";  -- R1 <- M[0036]
    tempo(5) := x"36";
    tempo(6) := x"00";

    tempo(7) := x"44";  -- R1 <- R0 - R1

    tempo(8) := x"81";  -- JZ 0011
    tempo(9) := x"11";
    tempo(10) := x"00";

    tempo(11) := x"47";  -- R1 <- 02
    tempo(12) := x"02";
    
    tempo(13) := x"71";  -- M[0037] <- R1
    tempo(14) := x"37";
    tempo(15) := x"00";

    tempo(16) := x"FF";  -- FIN
    
    tempo(17) := x"47";  -- R1 <- 01
    tempo(18) := x"01";
    
    tempo(19) := x"71";  -- M[0037] <- R1
    tempo(20) := x"37";
    tempo(21) := x"00";

    tempo(22) := x"FF";  -- FIN

    tempo(16#035#) := x"A4";
    tempo(16#036#) := x"A4";
    tempo(16#037#) := x"C6";
    
    return tempo;
  end inicia_ram5;

	function inicia_ram6 return banco is 
		variable tempo : banco := (others => (others => '0'));
	begin 
		for addr in 0 to 2 ** n_dir - 1 loop 
			-- Inicializa cada celda con el valor de su direccion
			tempo(addr) := std_logic_vector(to_unsigned(addr, N));
		end loop;
		-- Cambia las celdas donde esta el programa
		tempo(0) := x"70";	-- R1 <- M[1234]
		tempo(1) := x"34";
		tempo(2) := x"12";

		tempo(3) := x"71";	-- M[5678] <- R1
		tempo(4) := x"78";	
		tempo(5) := x"56";

		tempo(6) := x"45";  -- R1 <- R0 + R1
        
		tempo(7) := x"46";	-- R0 <- R1

		tempo(8) := x"47";	-- R1 <- 9A
		tempo(9) := x"9A";
        
		tempo(10) := x"80"; -- GOTO 0003
		tempo(11) := x"03";
		tempo(12) := x"00";
		
		tempo(13) := x"FF";	-- FIN (no se ejecuta por el salto previo)
        
		tempo(34) := x"86"; -- dato 
        
		tempo(78) := x"86"; -- dato

		
		return tempo;
	end inicia_ram6;
  
  signal contenido: banco; -- := inicia_ram;
  signal midir: std_logic_vector (dir'range);
  signal midatos: std_logic_vector (datos'range);
begin
  escritura: process (inicia, clk, cs, we, dir, datos)
    begin
    if inicia = '1' then
      -- null;
      contenido <= inicia_ram6;
    elsif (clk'event and clk = '1') then
      if (cs = '0' and we = '1') then
        contenido (to_integer (unsigned (dir))) <= datos;
      end if;
    end if;
    -- debiera ser sincrono
    midir <= dir;
  end process;

  lectura: process (oe, cs, contenido, midir) is
  begin
    if (cs = '0' and oe = '0') then
      datos <= contenido (to_integer (unsigned (midir)));
    else
      datos <= (others => 'Z');
    end if;    
  end process;
end architecture comportamiento;

// VHDL entity control, as the project stores it:
library ieee;
use ieee.std_logic_1164.all;
use ieee.numeric_std.all;

entity control is
  port (
    clk: in std_logic;
    rst: in std_logic;
    Flags: in std_logic_vector (7 downto 0);
    CO: in std_logic_vector (7 downto 0);
    clear: out std_logic;
    Lpc, Ipc, SelDir: out std_logic;
    inicia, cs, oe, we: out std_logic;
    LH, LL, Lri: out std_logic;
    SelRegW, SelRegRA, SelRegRB: out std_logic_vector (2 downto 0);
    wr: out std_logic;
    ope: out std_logic_vector (2 downto 0);
    SalAlu, LF: out std_logic;
    fin: out std_logic;
    idEstado: out std_logic_vector (4 downto 0)
  );
end entity control;

architecture una of control is
end architecture una;
