// Logisim project Procesador_completo.circ as structural Verilog
module main (
);

  wire alu_1_c, alu_1_s, alu_1_z, buffer_triestado_1_oe, clear, clk, control_1_p1, control_1_p2,
       control_1_p3, control_1_p23, cs, fin, inicia, Ipc, LF, LH1, LL, Lpc, Lri, oe, SalAlu, SelDir,
       undriven_2, undriven_3, undriven_4, undriven_5, we, wr;
  wire [2:0] ope, SelRegRA, SelRegRB, SelRegW;
  wire [7:0] buffer_triestado_1_salida, BusDatos, CO, din, dout, EntDat, registro_flags_1_flags_out, SalA,
       SalB, SalidaALU, undriven;
  wire [15:0] dir, SalidaHL, SalidaPC;

  // control control_1: pin names not known; wires that end beside it: control_1_p1, control_1_p2, control_1_p3, clear, Lpc, Ipc, SelDir, inicia, cs, oe, we, LH1, LL, Lri, SelRegW, SelRegRA, SelRegRB, wr, ope, SalAlu, LF, fin, control_1_p23
  banco_registros banco_registros_1 (
    .clk(clk), .clear(clear), .wr(wr), .SelRegW(SelRegW), .SelRegRA(SelRegRA), .SelRegRB(SelRegRB),
    .entDat(EntDat), .SalA(SalA), .SalB(SalB));
  // Probe on control_1_p23
  memoria_ram memoria_ram_1 (.clk(clk), .we(we), .cs(cs), .oe(oe), .inicia(inicia), .dir(dir), .din(din), .dout(dout));
  pc pc_1 (.clk(clk), .clear(clear), .Lpc(Lpc), .Ipc(Ipc), .EntradaPC(SalidaHL), .salidaPC(SalidaPC));
  registro_hl registro_hl_1 (.clk(clk), .clear(clear), .LH1(LH1), .LL(LL), .BusDatos_in(BusDatos), .SalidaHL(SalidaHL));
  registro_instruccion registro_instruccion_1 (.clk(clk), .clear(clear), .Lri(Lri), .BusDatos_in(BusDatos), .CO(CO));
  alu alu_1 (.SalA(SalA), .SalB(SalB), .ope(ope), .SalidaALU(SalidaALU), .Z(alu_1_z), .S(alu_1_s), .C(alu_1_c));
  registro_flags registro_flags_1 (
    .clk(clk), .clear(clear), .Lf(LF), .Z_in(undriven_3), .S_in(undriven_4), .C_in(undriven_5),
    .Flags_out(registro_flags_1_flags_out));
  mux_direcciones mux_direcciones_1 (.SelDir(SelDir), .salidaPC(SalidaPC), .SalidaHL(SalidaHL), .dir(dir));
  buffer_triestado buffer_triestado_1 (
    .entrada(undriven), .habilitar(undriven_2), .salida(buffer_triestado_1_salida), .oe(buffer_triestado_1_oe));
endmodule

// VHDL entity pc, as the project stores it:
library ieee;
use ieee.std_logic_1164.all;
use ieee.numeric_std.all;

entity pc is
    port (
        clk       : in  std_logic;
        clear     : in  std_logic;
        Lpc       : in  std_logic;
        Ipc       : in  std_logic;
        EntradaPC : in  std_logic_vector(15 downto 0);
        salidaPC  : out std_logic_vector(15 downto 0)
    );
end entity pc;

architecture rtl of pc is
    constant ADDR_WIDTH : integer := 16;
    signal cuenta : unsigned(ADDR_WIDTH-1 downto 0);
begin
    process(clk)
    begin
        if rising_edge(clk) then
            if clear = '1' then
                cuenta <= (others => '0');
            elsif Lpc = '1' then
                cuenta <= unsigned(EntradaPC);
            elsif Ipc = '1' then
                cuenta <= cuenta + 1;
            end if;
        end if;
    end process;

    salidaPC <= std_logic_vector(cuenta);
end architecture rtl;

// VHDL entity registro_instruccion, as the project stores it:
library ieee;
use ieee.std_logic_1164.all;

entity registro_instruccion is
    port (
        clk         : in  std_logic;
        clear       : in  std_logic;
        Lri         : in  std_logic;
        BusDatos_in : in  std_logic_vector(7 downto 0);
        CO          : out std_logic_vector(7 downto 0)
    );
end entity registro_instruccion;

architecture rtl of registro_instruccion is
    constant DATA_WIDTH : integer := 8;
begin
    process(clk)
    begin
        if rising_edge(clk) then
            if clear = '1' then
                CO <= (others => '0');
            elsif Lri = '1' then
                CO <= BusDatos_in;
            end if;
        end if;
    end process;
end architecture rtl;

// VHDL entity registro_hl, as the project stores it:
library ieee;
use ieee.std_logic_1164.all;

entity registro_hl is
    port (
        clk         : in  std_logic;
        clear       : in  std_logic;
        LH1         : in  std_logic;
        LL          : in  std_logic;
        BusDatos_in : in  std_logic_vector(7 downto 0);
        SalidaHL    : out std_logic_vector(15 downto 0)
    );
end entity registro_hl;

architecture rtl of registro_hl is
    constant DATA_WIDTH : integer := 8;
    signal H, L : std_logic_vector(DATA_WIDTH-1 downto 0);
begin
    process(clk)
    begin
        if rising_edge(clk) then
            if clear = '1' then
                H <= (others => '0');
                L <= (others => '0');
            else
                if LH1 = '1' then H <= BusDatos_in; end if;
                if LL  = '1' then L <= BusDatos_in; end if;
            end if;
        end if;
    end process;

    SalidaHL <= H & L;
end architecture rtl;

// VHDL entity mux_direcciones, as the project stores it:
library ieee;
use ieee.std_logic_1164.all;

entity mux_direcciones is
    port (
        SelDir   : in  std_logic;
        salidaPC : in  std_logic_vector(15 downto 0);
        SalidaHL : in  std_logic_vector(15 downto 0);
        dir      : out std_logic_vector(15 downto 0)
    );
end entity mux_direcciones;

architecture rtl of mux_direcciones is
begin
    dir <= salidaPC when SelDir = '0' else SalidaHL;
end architecture rtl;

// VHDL entity banco_registros, as the project stores it:
library ieee;
use ieee.std_logic_1164.all;
use ieee.numeric_std.all;

entity banco_registros is
    port (
        clk      : in  std_logic;
        clear    : in  std_logic;
        wr       : in  std_logic;
        SelRegW  : in  std_logic_vector(2 downto 0);
        SelRegRA : in  std_logic_vector(2 downto 0);
        SelRegRB : in  std_logic_vector(2 downto 0);
        entDat   : in  std_logic_vector(7 downto 0);
        SalA     : out std_logic_vector(7 downto 0);
        SalB     : out std_logic_vector(7 downto 0)
    );
end entity banco_registros;

architecture rtl of banco_registros is
    constant DATA_WIDTH     : integer := 8;
    constant REG_ADDR_WIDTH : integer := 3;

    type registro_array is array (0 to (2**REG_ADDR_WIDTH)-1) of std_logic_vector(DATA_WIDTH-1 downto 0);
    signal registros : registro_array;
begin
    SalA <= registros(to_integer(unsigned(SelRegRA)));
    SalB <= registros(to_integer(unsigned(SelRegRB)));

    process(clk)
    begin
        if rising_edge(clk) then
            if clear = '1' then
                for i in 0 to (2**REG_ADDR_WIDTH)-1 loop
                    registros(i) <= (others => '0');
                end loop;
            elsif wr = '1' then
                registros(to_integer(unsigned(SelRegW))) <= entDat;
            end if;
        end if;
    end process;
end architecture rtl;

// VHDL entity alu, as the project stores it:
library ieee;
use ieee.std_logic_1164.all;
use ieee.numeric_std.all;

entity alu is
    port (
        SalA      : in  std_logic_vector(7 downto 0);
        SalB      : in  std_logic_vector(7 downto 0);
        ope       : in  std_logic_vector(2 downto 0);
        SalidaALU : out std_logic_vector(7 downto 0);
        Z         : out std_logic;
        S         : out std_logic;
        C         : out std_logic
    );
end entity alu;

architecture rtl of alu is
    constant DATA_WIDTH : integer := 8;
begin
    process(SalA, SalB, ope)
        variable res_9bit : unsigned(DATA_WIDTH downto 0);
        variable a_9bit   : unsigned(DATA_WIDTH downto 0);
        variable b_9bit   : unsigned(DATA_WIDTH downto 0);
        variable res_8bit : std_logic_vector(DATA_WIDTH-1 downto 0);
    begin
        a_9bit := unsigned('0' & SalA);
        b_9bit := unsigned('0' & SalB);
        res_9bit := (others => '0');

        case ope is
            when "000" => res_9bit := a_9bit;
            when "001" => res_9bit := a_9bit xor b_9bit; res_9bit(DATA_WIDTH) := '0';
            when "010" => res_9bit := a_9bit and b_9bit;
            when "011" => res_9bit := not a_9bit;        res_9bit(DATA_WIDTH) := '0';
            when "100" => res_9bit := a_9bit - 1;
            when "101" => res_9bit := a_9bit + b_9bit;
            when "110" => res_9bit := a_9bit - b_9bit;
            when "111" => res_9bit := a_9bit + 1;
            when others => res_9bit := a_9bit;
        end case;

        res_8bit := std_logic_vector(res_9bit(DATA_WIDTH-1 downto 0));
        SalidaALU <= res_8bit;

        if res_8bit = x"00" then Z <= '1'; else Z <= '0'; end if;
        S <= res_8bit(DATA_WIDTH-1);

        if (ope = "100") or (ope = "110") then
            C <= res_9bit(DATA_WIDTH);
        elsif (ope = "101") or (ope = "111") then
            C <= res_9bit(DATA_WIDTH);
        else
            C <= '0';
        end if;
    end process;
end architecture rtl;

// VHDL entity buffer_triestado, as the project stores it:
library ieee;
use ieee.std_logic_1164.all;

entity buffer_triestado is
    port (
        entrada   : in  std_logic_vector(7 downto 0);
        habilitar : in  std_logic;
        salida    : out std_logic_vector(7 downto 0);
        oe        : out std_logic
    );
end entity buffer_triestado;

architecture rtl of buffer_triestado is
begin
    salida <= entrada;
    oe     <= habilitar;
end architecture rtl;

// VHDL entity registro_flags, as the project stores it:
library ieee;
use ieee.std_logic_1164.all;

entity registro_flags is
    port (
        clk       : in  std_logic;
        clear     : in  std_logic;
        Lf        : in  std_logic;
        Z_in      : in  std_logic;
        S_in      : in  std_logic;
        C_in      : in  std_logic;
        Flags_out : out std_logic_vector(7 downto 0)
    );
end entity registro_flags;

architecture rtl of registro_flags is
    signal reg : std_logic_vector(7 downto 0);
begin
    process(clk)
    begin
        if rising_edge(clk) then
            if clear = '1' then
                reg <= (others => '0');
            elsif Lf = '1' then
                reg(0) <= Z_in;
                reg(1) <= S_in;
                reg(2) <= C_in;
                reg(7 downto 3) <= (others => '0');
            end if;
        end if;
    end process;

    Flags_out <= reg;
end architecture rtl;

// VHDL entity memoria_ram, as the project stores it:
library ieee;
use ieee.std_logic_1164.all;
use ieee.numeric_std.all;

entity memoria_ram is
    port (
        clk    : in  std_logic;
        we     : in  std_logic;
        cs     : in  std_logic;
        oe     : in  std_logic;
        inicia : in  std_logic;
        dir    : in  std_logic_vector(15 downto 0);

        din    : in  std_logic_vector(7 downto 0);
        dout   : out std_logic_vector(7 downto 0)
    );
end entity memoria_ram;

architecture rtl of memoria_ram is
    constant DATA_WIDTH : integer := 8;

    type banco is array (0 to 255) of std_logic_vector(DATA_WIDTH-1 downto 0);

    function inicia_ram return banco is
        variable tempo : banco := (others => (others => '0'));
    begin
        for addr in 0 to 255 loop
            tempo(addr) := std_logic_vector(to_unsigned(addr, DATA_WIDTH));
        end loop;

        tempo(0)  := x"70"; tempo(1)  := x"35"; tempo(2)  := x"00";
        tempo(3)  := x"46";
        tempo(4)  := x"47"; tempo(5)  := x"5E";
        tempo(6)  := x"45";
        tempo(7)  := x"71"; tempo(8)  := x"36"; tempo(9)  := x"00";
        tempo(10) := x"82"; tempo(11) := x"0F"; tempo(12) := x"00";
        tempo(13) := x"10"; tempo(14) := x"20";
        tempo(15) := x"42";
        tempo(16) := x"81"; tempo(17) := x"2C"; tempo(18) := x"00";
        tempo(19) := x"42";
        tempo(20) := x"81"; tempo(21) := x"19"; tempo(22) := x"00";
        tempo(23) := x"11"; tempo(24) := x"21";
        tempo(25) := x"43";
        tempo(26) := x"40";
        tempo(27) := x"83"; tempo(28) := x"20"; tempo(29) := x"00";
        tempo(30) := x"12"; tempo(31) := x"22";
        tempo(32) := x"47"; tempo(33) := x"F9";
        tempo(34) := x"41";
        tempo(35) := x"70"; tempo(36) := x"36"; tempo(37) := x"00";
        tempo(38) := x"80"; tempo(39) := x"2C"; tempo(40) := x"00";
        tempo(44) := x"FF";

        tempo(16#035#) := x"A4";
        tempo(16#036#) := x"B5";
        tempo(16#037#) := x"C6";
        return tempo;
    end function;

    signal contenido : banco := inicia_ram;
    signal addr8 : integer range 0 to 255;
begin
    addr8 <= to_integer(unsigned(dir(7 downto 0)));

    process(clk)
    begin
        if rising_edge(clk) then
            if inicia = '1' then
                contenido <= inicia_ram;
            elsif (cs = '0') and (we = '1') then
                contenido(addr8) <= din;
            end if;
        end if;
    end process;

    dout <= contenido(addr8) when (cs = '0') and (oe = '0') else (others => '0');
end architecture rtl;

// VHDL entity control, as the project stores it:
library ieee;
use ieee.std_logic_1164.all;
use ieee.numeric_std.all;

entity control is
  port (
    clk      : in  std_logic;
    rst      : in  std_logic;
    Flags    : in  std_logic_vector(7 downto 0);
    CO       : in  std_logic_vector(7 downto 0);

    clear    : out std_logic;
    Lpc      : out std_logic;
    Ipc      : out std_logic;
    SelDir   : out std_logic;

    inicia   : out std_logic;
    cs       : out std_logic;
    oe       : out std_logic;
    we       : out std_logic;

    LH1      : out std_logic;  -- << consistente con registro_hl y ruta_datos
    LL       : out std_logic;
    Lri      : out std_logic;

    SelRegW  : out std_logic_vector(2 downto 0);
    SelRegRA : out std_logic_vector(2 downto 0);
    SelRegRB : out std_logic_vector(2 downto 0);
    wr       : out std_logic;

    ope      : out std_logic_vector(2 downto 0);
    SalAlu   : out std_logic;
    LF       : out std_logic;
    fin      : out std_logic;

    idEstado : out std_logic_vector(4 downto 0)
  );
end entity control;

architecture una of control is

  type state_type is (
    S00, S01, S02, S03, S04, S05, S06, S07, S08, S09,
    S10, S11, S12, S13, S14, S15, S16, S17, S18, S19, S20
  );

  signal current_state, next_state : state_type;

  alias FZ : std_logic is Flags(0);
  alias FS : std_logic is Flags(1);
  alias FC : std_logic is Flags(2);

  function state_to_slv(s : state_type) return std_logic_vector is
    variable v : unsigned(4 downto 0);
  begin
    case s is
      when S00 => v := to_unsigned(0, 5);
      when S01 => v := to_unsigned(1, 5);
      when S02 => v := to_unsigned(2, 5);
      when S03 => v := to_unsigned(3, 5);
      when S04 => v := to_unsigned(4, 5);
      when S05 => v := to_unsigned(5, 5);
      when S06 => v := to_unsigned(6, 5);
      when S07 => v := to_unsigned(7, 5);
      when S08 => v := to_unsigned(8, 5);
      when S09 => v := to_unsigned(9, 5);
      when S10 => v := to_unsigned(10, 5);
      when S11 => v := to_unsigned(11, 5);
      when S12 => v := to_unsigned(12, 5);
      when S13 => v := to_unsigned(13, 5);
      when S14 => v := to_unsigned(14, 5);
      when S15 => v := to_unsigned(15, 5);
      when S16 => v := to_unsigned(16, 5);
      when S17 => v := to_unsigned(17, 5);
      when S18 => v := to_unsigned(18, 5);
      when S19 => v := to_unsigned(19, 5);
      when S20 => v := to_unsigned(20, 5);
    end case;
    return std_logic_vector(v);
  end function;

begin

  idEstado <= state_to_slv(current_state);

  process(clk, rst)
  begin
    if rst = '1' then
      current_state <= S00;
    elsif rising_edge(clk) then
      current_state <= next_state;
    end if;
  end process;

  process(current_state, CO, FZ, FS, FC)
  begin
    -- defaults
    clear    <= '0';
    Lpc      <= '0';
    Ipc      <= '0';
    SelDir   <= '0';
    inicia   <= '0';

    cs       <= '1';
    oe       <= '1';
    we       <= '0';

    LH1      <= '0';
    LL       <= '0';
    Lri      <= '0';

    SelRegW  <= "000";
    SelRegRA <= "000";
    SelRegRB <= "000";
    wr       <= '0';

    ope      <= "000";
    SalAlu   <= '0';
    LF       <= '0';
    fin      <= '0';

    next_state <= current_state;

    case current_state is

      when S00 =>
        clear  <= '1';
        inicia <= '1';
        next_state <= S01;

      when S01 =>
        cs  <= '0';
        oe  <= '0';
        Lri <= '1';
        next_state <= S02;

      when S02 =>
        Ipc <= '1';
        case CO is
          when x"70" | x"71" | x"80" | x"81" | x"82" | x"83" =>
            next_state <= S03;

          when x"40" => next_state <= S15; -- NOT
          when x"41" => next_state <= S16; -- AND
          when x"42" => next_state <= S17; -- DEC
          when x"43" => next_state <= S18; -- INC
          when x"44" => next_state <= S19; -- SUB
          when x"45" => next_state <= S09; -- ADD
          when x"46" => next_state <= S10; -- MOV
          when x"30" => next_state <= S20; -- XOR
          when x"47" => next_state <= S12; -- MOVI
          when x"FF" => next_state <= S11; -- HALT

          when others =>
            next_state <= S01;
        end case;

      when S03 =>
        cs <= '0';
        oe <= '0';
        LL <= '1';
        next_state <= S04;

      when S04 =>
        Ipc <= '1';
        next_state <= S05;

      when S05 =>
        cs  <= '0';
        oe  <= '0';
        LH1 <= '1';
        next_state <= S06;

      when S06 =>
        Ipc <= '1';
        case CO is
          when x"70" => next_state <= S07; -- LOAD
          when x"71" => next_state <= S08; -- STORE
          when x"80" => next_state <= S14; -- JMP

          when x"81" => -- JZ
            if FZ = '1' then next_state <= S14; else next_state <= S01; end if;

          when x"82" => -- JC
            if FC = '1' then next_state <= S14; else next_state <= S01; end if;

          when x"83" => -- JS
            if FS = '1' then next_state <= S14; else next_state <= S01; end if;

          when others =>
            next_state <= S01;
        end case;

      when S07 => -- LOAD: R1 <- M(HL)
        SelDir  <= '1';
        cs      <= '0';
        oe      <= '0';
        SelRegW <= "001";
        wr      <= '1';
        next_state <= S01;

      when S08 => -- STORE: M(HL) <- R1
        SelDir   <= '1';
        cs       <= '0';
        we       <= '1';
        SelRegRA <= "001";
        ope      <= "000";
        SalAlu   <= '1';
        next_state <= S01;

      when S14 => -- JUMP: PC <- HL
        Lpc <= '1';
        next_state <= S01;

      when S09 => -- ADD: R1 <- R0 + R1
        SelRegW  <= "001";
        SelRegRA <= "000";
        SelRegRB <= "001";
        ope      <= "101";
        SalAlu   <= '1';
        wr       <= '1';
        LF       <= '1';
        next_state <= S01;

      when S10 => -- MOV: R0 <- R1
        SelRegW  <= "000";
        SelRegRA <= "001";
        ope      <= "000";
        SalAlu   <= '1';
        wr       <= '1';
        next_state <= S01;

      when S12 => -- MOVI: R1 <- M(PC)
        cs      <= '0';
        oe      <= '0';
        SelRegW <= "001";
        wr      <= '1';
        next_state <= S13;

      when S13 =>
        Ipc <= '1';
        next_state <= S01;

      when S15 => -- NOT
        SelRegW  <= "001";
        SelRegRA <= "001";
        ope      <= "011";
        SalAlu   <= '1';
        wr       <= '1';
        LF       <= '1';
        next_state <= S01;

      when S16 => -- AND
        SelRegW  <= "001";
        SelRegRA <= "000";
        SelRegRB <= "001";
        ope      <= "010";
        SalAlu   <= '1';
        wr       <= '1';
        LF       <= '1';
        next_state <= S01;

      when S17 => -- DEC
        SelRegW  <= "001";
        SelRegRA <= "001";
        ope      <= "100";
        SalAlu   <= '1';
        wr       <= '1';
        LF       <= '1';
        next_state <= S01;

      when S18 => -- INC
        SelRegW  <= "001";
        SelRegRA <= "001";
        ope      <= "111";
        SalAlu   <= '1';
        wr       <= '1';
        LF       <= '1';
        next_state <= S01;

      when S19 => -- SUB
        SelRegW  <= "001";
        SelRegRA <= "000";
        SelRegRB <= "001";
        ope      <= "110";
        SalAlu   <= '1';
        wr       <= '1';
        LF       <= '1';
        next_state <= S01;

      when S20 => -- XOR
        SelRegW  <= "001";
        SelRegRA <= "000";
        SelRegRB <= "001";
        ope      <= "001";
        SalAlu   <= '1';
        wr       <= '1';
        LF       <= '1';
        next_state <= S01;

      when S11 =>
        fin <= '1';
        next_state <= S11;

      when others =>
        next_state <= S00;

    end case;
  end process;

end architecture una;
