// Logisim project codificadorBG.circ as structural Verilog: 4 circuits, main circuit main
module main (
  input  SYS,
  input  N,
  input  CLK,
  input  RST,
  output out_5
);

  wire logica_estado_sig_1_j0, logica_estado_sig_1_j1, logica_estado_sig_1_k0, logica_estado_sig_1_k1,
       registro_estado_1_q0, registro_estado_1_q1;

  LOGICA_ESTADO_SIG logica_estado_sig_1 (
    .Q0(registro_estado_1_q0), .Q1(registro_estado_1_q1), .SYS(SYS), .N(N), .J0(logica_estado_sig_1_j0),
    .K0(logica_estado_sig_1_k0), .J1(logica_estado_sig_1_j1), .K1(logica_estado_sig_1_k1));
  REGISTRO_ESTADO registro_estado_1 (
    .J0(logica_estado_sig_1_j0), .K0(logica_estado_sig_1_k0), .J1(logica_estado_sig_1_j1),
    .K1(logica_estado_sig_1_k1), .CLK(CLK), .RST(RST), .Q0(registro_estado_1_q0), .Q1(registro_estado_1_q1));
  LOGICA_SALIDA logica_salida_1 (.Q0(registro_estado_1_q0), .Q1(registro_estado_1_q1), .C_BIT(out_5));
endmodule

module LOGICA_ESTADO_SIG (
  input  Q0,
  input  Q1,
  input  SYS,
  input  N,
  output J0,
  output K0,
  output J1,
  output K1
);

  wire and_1_out, and_2_out, and_3_out, and_4_out, and_5_out, and_6_out, not_1_out, not_2_out, not_3_out;

  not not_1 (not_1_out, Q1);
  not not_2 (not_2_out, SYS);
  not not_3 (not_3_out, N);
  and and_1 (and_1_out, not_2_out, N);
  and and_2 (and_2_out, SYS, not_3_out);
  and and_3 (and_3_out, not_1_out, N);
  and and_4 (and_4_out, Q1, not_3_out);
  and and_5 (and_5_out, not_1_out, not_3_out);
  and and_6 (and_6_out, Q1, N);
  or or_1 (K1, and_1_out, and_2_out);
  or or_2 (J0, and_3_out, and_4_out);
  or or_3 (K0, and_5_out, and_6_out);

  assign J1 = N;
endmodule

module LOGICA_SALIDA (
  input  Q0,
  input  Q1,
  output C_BIT
);


  assign C_BIT = Q0;
endmodule

module REGISTRO_ESTADO (
  input  J0,
  input  K0,
  input  J1,
  input  K1,
  input  CLK,
  input  RST,
  output Q0,
  output Q1
);

  J_K_Flip_Flop j_k_ff_1 (.J(J0), .K(K0), .clk(CLK), .Q(Q0), .reset(RST));  // open: Qn, preset
  J_K_Flip_Flop j_k_ff_2 (.J(J1), .K(K1), .clk(CLK), .Q(Q1), .reset(RST));  // open: Qn, preset
endmodule
