// Logisim project contador_cerosounos.circ as structural Verilog
module main (
  input  [6:0] in_1
);

  wire [6:0] cuenta_unos_o_ceros_1_cantidad, cuenta_unos_o_ceros_1_tipo;

  cuenta_unos_o_ceros cuenta_unos_o_ceros_1 (
    .a(in_1[0]), .b(in_1[1]), .c(in_1[2]), .d(in_1[3]), .e(in_1[4]), .f(in_1[5]), .g(in_1[6]),
    .cantidad(cuenta_unos_o_ceros_1_cantidad), .tipo(cuenta_unos_o_ceros_1_tipo));
  _7_Segment_Display u_7_segment_display_1 (
    .g(cuenta_unos_o_ceros_1_cantidad[6]), .f(cuenta_unos_o_ceros_1_cantidad[5]),
    .a(cuenta_unos_o_ceros_1_cantidad[0]), .b(cuenta_unos_o_ceros_1_cantidad[1]),
    .e(cuenta_unos_o_ceros_1_cantidad[4]), .d(cuenta_unos_o_ceros_1_cantidad[3]),
    .c(cuenta_unos_o_ceros_1_cantidad[2]));  // open: dp
  _7_Segment_Display u_7_segment_display_2 (
    .g(cuenta_unos_o_ceros_1_tipo[6]), .f(cuenta_unos_o_ceros_1_tipo[5]), .a(cuenta_unos_o_ceros_1_tipo[0]),
    .b(cuenta_unos_o_ceros_1_tipo[1]), .e(cuenta_unos_o_ceros_1_tipo[4]), .d(cuenta_unos_o_ceros_1_tipo[3]),
    .c(cuenta_unos_o_ceros_1_tipo[2]));  // open: dp
endmodule

// VHDL entity cuenta_unos_o_ceros, as the project stores it:
LIBRARY ieee;
USE ieee.std_logic_1164.all;
USE ieee.numeric_std.all;

ENTITY cuenta_unos_o_ceros IS
  PORT(
        a, b, c, d, e, f, g : IN  std_logic; -- 7 entradas (a: LSB, g: MSB)
        cantidad            : OUT std_logic_vector(6 DOWNTO 0); -- Display 1 (Conteo)
        tipo                : OUT std_logic_vector(6 DOWNTO 0)  -- Display 2 ('0' o '1')
  );  
END ENTITY cuenta_unos_o_ceros;

ARCHITECTURE una OF cuenta_unos_o_ceros IS

    -- Función para convertir un entero (0-7) al patrón de un display de 7 segmentos (g f e d c b a)
    FUNCTION decodificar_7seg(num : INTEGER) RETURN std_logic_vector IS
    BEGIN
        CASE num IS
            WHEN 0 => RETURN "0111111"; -- Muestra '0'
            WHEN 1 => RETURN "0000110"; -- Muestra '1'
            WHEN 2 => RETURN "1011011"; -- Muestra '2'
            WHEN 3 => RETURN "1001111"; -- Muestra '3'
            WHEN 4 => RETURN "1100110"; -- Muestra '4'
            WHEN 5 => RETURN "1101101"; -- Muestra '5'
            WHEN 6 => RETURN "1111101"; -- Muestra '6'
            WHEN 7 => RETURN "0000111"; -- Muestra '7'
            WHEN OTHERS => RETURN "0000000";
        END CASE;
    END FUNCTION;

BEGIN

    PROCESS(a, b, c, d, e, f, g) IS
        VARIABLE numero      : std_logic_vector(6 DOWNTO 0);
        VARIABLE unos, ceros : INTEGER RANGE 0 TO 7; 
        VARIABLE valor_mayor : INTEGER RANGE 0 TO 7;
    BEGIN
    
        ceros := 0;
        unos  := 0;
        
        -- Concatenación de las 7 entradas
        numero := g & f & e & d & c & b & a;
        
        FOR i IN 0 TO 6 LOOP
            IF numero(i) = '0' THEN
                ceros := ceros + 1; 
            ELSE 
                unos := unos + 1; 
            END IF;
        END LOOP;

        IF ceros > unos THEN
            valor_mayor := ceros;
            tipo        <= decodificar_7seg(0); -- Muestra el símbolo '0'
        ELSE 
            valor_mayor := unos;
            tipo        <= decodificar_7seg(1); -- Muestra el símbolo '1'
        END IF;
        
        cantidad <= decodificar_7seg(valor_mayor);
        
    END PROCESS;

END ARCHITECTURE una;
