// Logisim project contador_cerosounos_optimizado.circ as structural Verilog
module main (
  input  [6:0] in_1
);

  wire [6:0] cuenta_unos_o_ceros_1_cantidad, cuenta_unos_o_ceros_1_tipo;

  cuenta_unos_o_ceros cuenta_unos_o_ceros_1 (
    .a(in_1[0]), .b(in_1[1]), .c(in_1[2]), .d(in_1[3]), .e(in_1[4]), .f(in_1[5]), .g(in_1[6]),
    .cantidad(cuenta_unos_o_ceros_1_cantidad), .tipo(cuenta_unos_o_ceros_1_tipo));
  _7_Segment_Display u_7_segment_display_1 (
    .g(cuenta_unos_o_ceros_1_cantidad[6]), .f(cuenta_unos_o_ceros_1_cantidad[5]),
    .a(cuenta_unos_o_ceros_1_cantidad[0]), .b(cuenta_unos_o_ceros_1_cantidad[1]),
    .e(cuenta_unos_o_ceros_1_cantidad[4]), .d(cuenta_unos_o_ceros_1_cantidad[3]),
    .c(cuenta_unos_o_ceros_1_cantidad[2]));  // open: dp
  _7_Segment_Display u_7_segment_display_2 (
    .g(cuenta_unos_o_ceros_1_tipo[6]), .f(cuenta_unos_o_ceros_1_tipo[5]), .a(cuenta_unos_o_ceros_1_tipo[0]),
    .b(cuenta_unos_o_ceros_1_tipo[1]), .e(cuenta_unos_o_ceros_1_tipo[4]), .d(cuenta_unos_o_ceros_1_tipo[3]),
    .c(cuenta_unos_o_ceros_1_tipo[2]));  // open: dp
endmodule

// VHDL entity cuenta_unos_o_ceros, as the project stores it:
LIBRARY ieee;
USE ieee.std_logic_1164.all;

ENTITY cuenta_unos_o_ceros IS
  PORT(
        a, b, c, d, e, f, g : IN  std_logic;
        cantidad            : OUT std_logic_vector(6 DOWNTO 0); -- Display 1 (Conteo mayoritario)
        tipo                : OUT std_logic_vector(6 DOWNTO 0)  -- Display 2 ('0' o '1')
  );  
END ENTITY cuenta_unos_o_ceros;

ARCHITECTURE optimizada OF cuenta_unos_o_ceros IS
BEGIN

    PROCESS(a, b, c, d, e, f, g) IS
        VARIABLE entradas : std_logic_vector(6 DOWNTO 0);
        VARIABLE unos     : INTEGER RANGE 0 TO 7;
    BEGIN
        entradas := g & f & e & d & c & b & a;
        unos     := 0;
        
        -- Conteo único de unos (Popcount)
        FOR i IN 0 TO 6 LOOP
            IF entradas(i) = '1' THEN
                unos := unos + 1;
            END IF;
        END LOOP;

        -- 1. Determinar tipo (Mayoría)
        IF unos >= 4 THEN
            tipo <= "0000110"; -- Muestra '1' en display
        ELSE
            tipo <= "0111111"; -- Muestra '0' en display
        END IF;

        -- 2. Determinar cantidad aprovechando simetría
        CASE unos IS
            WHEN 0 | 7  => cantidad <= "0000111"; -- Muestra '7'
            WHEN 1 | 6  => cantidad <= "1111101"; -- Muestra '6'
            WHEN 2 | 5  => cantidad <= "1101101"; -- Muestra '5'
            WHEN OTHERS => cantidad <= "1100110"; -- Muestra '4' (Casos 3 y 4)
        END CASE;
        
    END PROCESS;

END ARCHITECTURE optimizada;
