// Logisim project unidad_control_logisim.circ as structural Verilog
module main (
  input  in_1,
  input  in_2,
  input  [7:0] in_3,
  input  [7:0] in_4,
  output out_5,
  output out_6,
  output out_7,
  output out_8,
  output out_9,
  output out_10,
  output out_11,
  output out_12,
  output out_13,
  output out_14,
  output out_15,
  output [2:0] out_16,
  output [2:0] out_17,
  output [2:0] out_18,
  output out_19,
  output [2:0] out_20,
  output out_21,
  output out_22,
  output out_23,
  output [4:0] out_24
);

  wire control_1_cs, control_1_oe;

  control control_1 (
    .clk(in_1), .rst(in_2), .Flags(in_3), .CO(in_4), .clear(out_5), .Lpc(out_6), .Ipc(out_7), .SelDir(out_8),
    .inicia(out_9), .cs(control_1_cs), .oe(control_1_oe), .we(out_12), .LH(out_13), .LL(out_14),
    .Lri(out_15), .SelRegW(out_16), .SelRegRA(out_17), .SelRegRB(out_18), .wr(out_19), .ope(out_20),
    .SalAlu(out_21), .LF(out_22), .fin(out_23), .idEstado(out_24));
  not not_1 (out_10, control_1_cs);
  not not_2 (out_11, control_1_oe);
endmodule

// VHDL entity control, as the project stores it:
library ieee;
use ieee.std_logic_1164.all;
use ieee.numeric_std.all;

-- ============================================================================
-- Entidad: control
-- Rol:
--   Unidad de Control basada en una Máquina de Estados Finitos (FSM) que
--   secuencia el ciclo FETCH–DECODE–EXECUTE de un procesador sencillo de 8 bits.
--
-- Entradas:
--   - clk : reloj del sistema.
--   - rst : reset externo (asíncrono) que fuerza el estado inicial.
--   - Flags[7:0] : banderas de estado (se usan Z,S,C en bits 0,1,2).
--   - CO[7:0] : código de operación (OpCode) proveniente del Registro de
--              Instrucción (RI).
--
-- Salidas:
--   Señales de control hacia datapath/memoria: clear, Lpc, Ipc, SelDir, inicia,
--   cs, oe, we, LH, LL, Lri, selectores de registros, wr, operación ALU (ope),
--   habilitación de bus (SalAlu), carga de flags (LF) y fin (HALT).
--   - idEstado[4:0] : codificación binaria del estado actual (debug/monitoreo).
--
-- Notas:
--   - cs y oe son ACTIVOS EN BAJO (0 => activo).
--   - we es ACTIVO EN ALTO (1 => escritura).
-- ============================================================================
entity control is
  port (
    clk: in std_logic;
    rst: in std_logic;
    Flags: in std_logic_vector (7 downto 0);
    CO: in std_logic_vector (7 downto 0);

    clear: out std_logic;
    Lpc, Ipc, SelDir: out std_logic;
    inicia, cs, oe, we: out std_logic;
    LH, LL, Lri: out std_logic;

    SelRegW, SelRegRA, SelRegRB: out std_logic_vector (2 downto 0);
    wr: out std_logic;

    ope: out std_logic_vector (2 downto 0);
    SalAlu, LF: out std_logic;
    fin: out std_logic;

    idEstado: out std_logic_vector (4 downto 0)
  );
end entity control;

architecture una of control is

  -- ==========================================================================
  -- Definición de estados:
  --   S00..S02  : fetch + decode inicial
  --   S03..S06  : lectura de operando de 16 bits (carga de HL)
  --   S07..S08  : acceso a memoria (LOAD/STORE)
  --   S09..S10  : ALU/transferencias rápidas (ADD, MOV)
  --   S12..S13  : inmediato (MOVI)
  --   S14       : salto (JMP/Jcc)
  --   S15..S20  : ALU lógicas/ariméticas (NOT, AND, DEC, INC, SUB, XOR)
  --   S11       : HALT
  -- ==========================================================================
  type state_type is (
    S00, S01, S02, S03, S04, S05, S06, S07, S08, S09,
    S10, S11, S12, S13, S14, S15, S16, S17, S18, S19, S20
  );

  -- Registro de estado actual y estado siguiente
  signal current_state, next_state : state_type;

  -- ==========================================================================
  -- Aliases de banderas:
  --   Se extraen bits específicos del vector Flags para saltos condicionales.
  -- ==========================================================================
  alias FZ : std_logic is Flags(0);  -- Zero flag
  alias FS : std_logic is Flags(1);  -- Sign flag
  alias FC : std_logic is Flags(2);  -- Carry flag

  -- ==========================================================================
  -- Función de mapeo: state_type -> std_logic_vector(4 downto 0)
  --   - Exporta el estado como número binario para depuración.
  --   - Se usa numeric_std para convertir con to_unsigned.
  -- ==========================================================================
  function state_to_slv(s : state_type) return std_logic_vector is
    variable v : unsigned(4 downto 0);
  begin
    case s is
      when S00 => v := to_unsigned(0, 5);
      when S01 => v := to_unsigned(1, 5);
      when S02 => v := to_unsigned(2, 5);
      when S03 => v := to_unsigned(3, 5);
      when S04 => v := to_unsigned(4, 5);
      when S05 => v := to_unsigned(5, 5);
      when S06 => v := to_unsigned(6, 5);
      when S07 => v := to_unsigned(7, 5);
      when S08 => v := to_unsigned(8, 5);
      when S09 => v := to_unsigned(9, 5);
      when S10 => v := to_unsigned(10, 5);
      when S11 => v := to_unsigned(11, 5);
      when S12 => v := to_unsigned(12, 5);
      when S13 => v := to_unsigned(13, 5);
      when S14 => v := to_unsigned(14, 5);
      when S15 => v := to_unsigned(15, 5);
      when S16 => v := to_unsigned(16, 5);
      when S17 => v := to_unsigned(17, 5);
      when S18 => v := to_unsigned(18, 5);
      when S19 => v := to_unsigned(19, 5);
      when S20 => v := to_unsigned(20, 5);
    end case;
    return std_logic_vector(v);
  end function;

begin

  -- ========================================================================
  -- Salida de estado (debug):
  --   idEstado refleja el estado ACTUAL (no el siguiente).
  -- ========================================================================
  idEstado <= state_to_slv(current_state);

  -- ========================================================================
  -- Proceso secuencial (registro de estado):
  --   - Reset asíncrono: cuando rst=1 se fuerza el estado inicial S00.
  --   - En flanco de subida de clk se transfiere next_state a current_state.
  -- ========================================================================
  process(clk, rst)
  begin
    if rst = '1' then
      current_state <= S00;
    elsif rising_edge(clk) then
      current_state <= next_state;
    end if;
  end process;

  -- ========================================================================
  -- Proceso combinacional (lógica de control):
  --   - Define valores por defecto para TODAS las salidas en cada evaluación,
  --     evitando inferencia de latches.
  --   - Implementa:
  --       * Función de transición de estados (next_state)
  --       * Función de salida (señales de control) tipo Moore/Mealy híbrida:
  --           - Principalmente Moore (depende del estado).
  --           - Saltos condicionales en S06 dependen de Flags (Mealy local).
  -- ========================================================================
  process(current_state, CO, FZ, FS, FC)
  begin
    -------------------------------------------------------------------------
    -- Defaults seguros:
    --   Todas las salidas desactivadas por defecto; memoria inactiva.
    -------------------------------------------------------------------------
    clear    <= '0';
    Lpc      <= '0';
    Ipc      <= '0';
    SelDir   <= '0';
    inicia   <= '0';

    cs       <= '1'; -- Chip Select RAM (activo bajo): 1 => deshabilitado
    oe       <= '1'; -- Output Enable (activo bajo): 1 => no leer al bus
    we       <= '0'; -- Write Enable (activo alto): 0 => no escribir

    LH       <= '0';
    LL       <= '0';
    Lri      <= '0';

    SelRegW  <= "000";
    SelRegRA <= "000";
    SelRegRB <= "000";
    wr       <= '0';

    ope      <= "000";
    SalAlu   <= '0';
    LF       <= '0';
    fin      <= '0';

    -- Permanecer en el mismo estado si no se especifica transición
    next_state <= current_state;

    case current_state is

      -----------------------------------------------------------------------
      -- S00: RESET/INIT
      --   - clear: reset interno del datapath (registros).
      --   - inicia: inicialización de memoria (si aplica).
      --   - Pasa a FETCH.
      -----------------------------------------------------------------------
      when S00 =>
        clear  <= '1';
        inicia <= '1';
        next_state <= S01;

      -----------------------------------------------------------------------
      -- S01: FETCH0
      --   - Lee memoria en la dirección apuntada por PC (SelDir por defecto=0).
      --   - cs/oe activos para colocar el OpCode en el bus.
      --   - Lri captura el OpCode en el Registro de Instrucción.
      -----------------------------------------------------------------------
      when S01 =>
        cs  <= '0';
        oe  <= '0';
        Lri <= '1';
        next_state <= S02;

      -----------------------------------------------------------------------
      -- S02: FETCH1 + DECODE
      --   - Incrementa PC (Ipc=1) para apuntar al siguiente byte.
      --   - Decodifica el OpCode (CO) para decidir la ruta de ejecución:
      --       * Instrucciones con operando de 16 bits -> rutina HL (S03)
      --       * Instrucciones de ALU de 1 ciclo -> estados S09..S20
      --       * MOVI -> S12 (carga inmediata)
      --       * HALT -> S11
      --       * Otros -> NOP/unknown => vuelve a S01
      --
      --   NOT  = x"40"
      --   XOR  = x"30"
      -----------------------------------------------------------------------
      when S02 =>
        Ipc <= '1';
        case CO is
          -- Requieren capturar dirección 16b (2 bytes) en HL
          when x"70" | x"71" | x"80" | x"81" | x"82" | x"83" =>
            next_state <= S03;

          when x"40" => -- NOT
            next_state <= S15;

          when x"41" => -- AND
            next_state <= S16;

          when x"42" => -- DEC
            next_state <= S17;

          when x"43" => -- INC
            next_state <= S18;

          when x"44" => -- SUB
            next_state <= S19;

          when x"45" => -- ADD
            next_state <= S09;

          when x"46" => -- MOV R0 <- R1
            next_state <= S10;

          when x"30" => -- XOR
            next_state <= S20;

          when x"47" => -- MOVI
            next_state <= S12;

          when x"FF" => -- HALT
            next_state <= S11;

          when others =>
            next_state <= S01;
        end case;

      -----------------------------------------------------------------------
      -- S03: Lee byte bajo de la dirección (PC apunta al low) y carga L
      --   - cs/oe habilitan lectura de RAM.
      --   - LL carga el registro L del par HL.
      -----------------------------------------------------------------------
      when S03 =>
        cs <= '0';
        oe <= '0';
        LL <= '1';
        next_state <= S04;

      -----------------------------------------------------------------------
      -- S04: Incrementa PC para apuntar al byte alto de la dirección.
      -----------------------------------------------------------------------
      when S04 =>
        Ipc <= '1';
        next_state <= S05;

      -----------------------------------------------------------------------
      -- S05: Lee byte alto de la dirección y carga H
      --   - cs/oe habilitan lectura de RAM.
      --   - LH carga el registro H del par HL.
      -----------------------------------------------------------------------
      when S05 =>
        cs <= '0';
        oe <= '0';
        LH <= '1';
        next_state <= S06;

      -----------------------------------------------------------------------
      -- S06: Incrementa PC para apuntar a la siguiente instrucción y sub-decodifica
      --   - Para LOAD/STORE ejecuta acceso a memoria usando HL.
      --   - Para saltos condicionales evalúa flags:
      --       JZ: FZ, JC: FC, JS: FS
      --   - JMP/Jcc tomada => S14 (cargar PC con HL)
      --   - No tomada => vuelve a FETCH (S01)
      -----------------------------------------------------------------------
      when S06 =>
        Ipc <= '1';
        case CO is
          when x"70" => -- LOAD
            next_state <= S07;
          when x"71" => -- STORE
            next_state <= S08;
          when x"80" => -- JMP incondicional
            next_state <= S14;

          when x"81" => -- JZ
            if FZ = '1' then next_state <= S14; else next_state <= S01; end if;

          when x"82" => -- JC
            if FC = '1' then next_state <= S14; else next_state <= S01; end if;

          when x"83" => -- JS
            if FS = '1' then next_state <= S14; else next_state <= S01; end if;

          when others =>
            next_state <= S01;
        end case;

      -----------------------------------------------------------------------
      -- S07: LOAD
      --   - SelDir=1 selecciona HL como dirección hacia la RAM.
      --   - cs/oe habilitan lectura; el dato va del bus a banco de registros.
      --   - wr=1 escribe en el banco; SelRegW="001" selecciona R1 destino.
      -----------------------------------------------------------------------
      when S07 =>
        SelDir  <= '1';
        cs      <= '0';
        oe      <= '0';
        SelRegW <= "001";
        wr      <= '1';
        next_state <= S01;

      -----------------------------------------------------------------------
      -- S08: STORE
      --   - SelDir=1 direcciona con HL.
      --   - cs=0 habilita chip; we=1 habilita escritura en RAM.
      --   - SelRegRA="001" selecciona R1 como fuente.
      --   - ope="000" (bypass) y SalAlu=1 ponen el dato al bus compartido
      --     a través del buffer triestado de la ALU (según tu datapath).
      -----------------------------------------------------------------------
      when S08 =>
        SelDir   <= '1';
        cs       <= '0';
        we       <= '1';
        SelRegRA <= "001";
        ope      <= "000";
        SalAlu   <= '1';
        next_state <= S01;

      -----------------------------------------------------------------------
      -- S14: JUMP (JMP/Jcc tomada)
      --   - Lpc=1 carga el PC con el valor del par HL (dirección destino).
      -----------------------------------------------------------------------
      when S14 =>
        Lpc <= '1';
        next_state <= S01;

      -----------------------------------------------------------------------
      -- S09: ADD  (R1 <- R0 + R1)
      --   - Selección operandos: RA=R0, RB=R1
      --   - ope="101" indica suma en ALU
      --   - SalAlu=1 habilita salida ALU al bus
      --   - wr=1 escribe resultado en R1
      --   - LF=1 captura flags Z/S/C en registro de banderas
      -----------------------------------------------------------------------
      when S09 =>
        SelRegW  <= "001";
        SelRegRA <= "000";
        SelRegRB <= "001";
        ope      <= "101";
        SalAlu   <= '1';
        wr       <= '1';
        LF       <= '1';
        next_state <= S01;

      -----------------------------------------------------------------------
      -- S10: MOV (R0 <- R1)
      --   - ope="000" bypass (pasar RA)
      --   - RA=R1, destino W=R0
      --   - wr=1 escribe en banco de registros
      --   - No actualiza flags (LF=0).
      -----------------------------------------------------------------------
      when S10 =>
        SelRegW  <= "000";
        SelRegRA <= "001";
        ope      <= "000";
        SalAlu   <= '1';
        wr       <= '1';
        next_state <= S01;

      -----------------------------------------------------------------------
      -- S12: MOVI (R1 <- M(PC))
      --   - Lee el inmediato desde memoria (cs/oe).
      --   - Banco de registros escribe directamente desde BusDatos (datapath),
      --     por eso SalAlu no se usa aquí.
      --   - Luego pasa a S13 para incrementar PC.
      -----------------------------------------------------------------------
      when S12 =>
        cs      <= '0';
        oe      <= '0';
        SelRegW <= "001";
        wr      <= '1';
        next_state <= S13;

      -----------------------------------------------------------------------
      -- S13: Ajuste PC tras MOVI
      --   - Ipc=1 para consumir el inmediato.
      -----------------------------------------------------------------------
      when S13 =>
        Ipc <= '1';
        next_state <= S01;

      -----------------------------------------------------------------------
      -- S15: NOT (R1 <- not R1)
      --   - RA=R1, ope="011" = NOT
      --   - escribe en R1 y actualiza flags
      -----------------------------------------------------------------------
      when S15 =>
        SelRegW  <= "001";
        SelRegRA <= "001";
        ope      <= "011";
        SalAlu   <= '1';
        wr       <= '1';
        LF       <= '1';
        next_state <= S01;

      -----------------------------------------------------------------------
      -- S16: AND (R1 <- R0 and R1)
      --   - RA=R0, RB=R1, ope="010" = AND
      --   - escribe en R1 y actualiza flags
      -----------------------------------------------------------------------
      when S16 =>
        SelRegW  <= "001";
        SelRegRA <= "000";
        SelRegRB <= "001";
        ope      <= "010";
        SalAlu   <= '1';
        wr       <= '1';
        LF       <= '1';
        next_state <= S01;

      -----------------------------------------------------------------------
      -- S17: DEC (R1 <- R1 - 1)
      --   - RA=R1, ope="100" = resta 1 (micro-op de ALU)
      -----------------------------------------------------------------------
      when S17 =>
        SelRegW  <= "001";
        SelRegRA <= "001";
        ope      <= "100";
        SalAlu   <= '1';
        wr       <= '1';
        LF       <= '1';
        next_state <= S01;

      -----------------------------------------------------------------------
      -- S18: INC (R1 <- R1 + 1)
      --   - RA=R1, ope="111" = suma 1
      -----------------------------------------------------------------------
      when S18 =>
        SelRegW  <= "001";
        SelRegRA <= "001";
        ope      <= "111";
        SalAlu   <= '1';
        wr       <= '1';
        LF       <= '1';
        next_state <= S01;

      -----------------------------------------------------------------------
      -- S19: SUB (R1 <- R0 - R1)
      --   - RA=R0, RB=R1, ope="110" = resta
      -----------------------------------------------------------------------
      when S19 =>
        SelRegW  <= "001";
        SelRegRA <= "000";
        SelRegRB <= "001";
        ope      <= "110";
        SalAlu   <= '1';
        wr       <= '1';
        LF       <= '1';
        next_state <= S01;

      -----------------------------------------------------------------------
      -- S20: XOR (R1 <- R0 xor R1)
      --   - RA=R0, RB=R1, ope="001" = XOR
      -----------------------------------------------------------------------
      when S20 =>
        SelRegW  <= "001";
        SelRegRA <= "000";
        SelRegRB <= "001";
        ope      <= "001";
        SalAlu   <= '1';
        wr       <= '1';
        LF       <= '1';
        next_state <= S01;

      -----------------------------------------------------------------------
      -- S11: HALT
      --   - fin=1 indica detención.
      --   - next_state se mantiene en S11 (bucle estable).
      -----------------------------------------------------------------------
      when S11 =>
        fin <= '1';
        next_state <= S11;

      -- Estado por defecto de recuperación
      when others =>
        next_state <= S00;
    end case;
  end process;

end architecture una;
