// Logisim project vumetro8bits.circ as structural Verilog
module main (
);

  wire [7:0] slider_1_out, vumetro_8bits_1_sal;

  Slider slider_1 (.out(slider_1_out));
  vumetro_8bits vumetro_8bits_1 (.ent(slider_1_out), .sal(vumetro_8bits_1_sal));
  LedBar ledbar_1 (
    .led0(vumetro_8bits_1_sal[7]), .led1(vumetro_8bits_1_sal[6]), .led2(vumetro_8bits_1_sal[5]),
    .led3(vumetro_8bits_1_sal[4]), .led4(vumetro_8bits_1_sal[3]), .led5(vumetro_8bits_1_sal[2]),
    .led6(vumetro_8bits_1_sal[1]), .led7(vumetro_8bits_1_sal[0]));
endmodule

// VHDL entity vumetro_8bits, as the project stores it:
LIBRARY ieee;
USE ieee.std_logic_1164.all;
USE ieee.numeric_std.all;

ENTITY vumetro_8bits IS
  PORT (
       ent   : IN  STD_LOGIC_VECTOR(7 DOWNTO 0); 
       sal   : OUT STD_LOGIC_VECTOR(7 DOWNTO 0)  
    );
END ENTITY vumetro_8bits;

ARCHITECTURE una OF vumetro_8bits IS

BEGIN

	PROCESS(ent) IS 
		VARIABLE entrada : INTEGER RANGE 0 TO 255;
	BEGIN

	entrada := to_integer(unsigned(ent));

	if entrada = 0 then
		sal <= X"00";
	elsif entrada <= 32 then
		sal <= X"01";
	elsif entrada <= 64 then
		sal <= X"03";
	elsif entrada <= 96 then
		sal <= X"07";
	elsif entrada <= 128 then
		sal <= X"0F";			  
	elsif entrada <= 160 then
		sal <= X"1F";
	elsif entrada <= 192 then
		sal <= X"3F";
	elsif entrada <= 224 then
		sal <= X"7F";
	else 
		sal <= X"FF";
		
	end if;
			
	END PROCESS;

END ARCHITECTURE una;
