// Logisim project PROCESADOR_VHDL.circ as structural Verilog
module main (
  input  in_1,
  input  in_2,
  output [4:0] out_3
);

  wire CLK, Fin, Ipc, Lf, LH, LL, Lpc, Lri, oe, SalAlu, SelDir, we, wr;
  wire [2:0] ope, SelRegRA, SelRegRB, SelRegW;
  wire [7:0] alu_1_salidaflags, br_1_sala, br_1_salb, BusDatos, CO, dirH, dirL, FLGS, SalidaALU;
  wire [15:0] dir, entradaPC, pc_1_salida;

  Clock clock_1 (.out(CLK));
  // Probe on CO
  // Probe on dirL
  // Probe on SalidaALU
  // Probe on BusDatos
  // Probe on Fin
  // Probe on BusDatos
  PC pc_1 (.Lpc(Lpc), .entradaPC(entradaPC), .Ipc(Ipc), .CLK(CLK), .CLEAR(in_1), .salida(pc_1_salida));
  HL hl_1 (.LL(LL), .LH(LH), .BusDatos(BusDatos), .CLK(CLK), .CLEAR(in_1), .SalidaHL(entradaPC));
  BR br_1 (
    .entDat(BusDatos), .SelRegRA(SelRegRA), .wr(wr), .SelRegW(SelRegW), .SelRegRB(SelRegRB), .CLK(CLK),
    .CLEAR(in_1), .SalA(br_1_sala), .SalB(br_1_salb));
  unidad_control unidad_control_1 (
    .clk(CLK), .rst(in_2), .CO(CO), .FLGS(FLGS), .Lpc(Lpc), .Ipc(Ipc), .SelDir(SelDir), .LH(LH), .LL(LL),
    .Lri(Lri), .SelRegW(SelRegW), .wr(wr), .SelRegRA(SelRegRA), .SelRegRB(SelRegRB), .ope(ope),
    .SalAlu(SalAlu), .LF(Lf), .oe(oe), .we(we), .Fin(Fin), .estado_out(out_3));
  MUXPCHL muxpchl_1 (
    .SalidaPC(pc_1_salida), .SalidaHL(entradaPC), .SelDir(SelDir), .dir(dir), .dirL(dirL), .dirH(dirH));
  ALU alu_1 (.SalA(br_1_sala), .SalB(br_1_salb), .ope(ope), .SalidaALU(SalidaALU), .SalidaFlags(alu_1_salidaflags));
  MEMORIA memoria_1 (.dirL(dirL), .we(we), .oe(oe), .CLK(CLK), .datos(BusDatos));
  RI ri_1 (.BusDatos(BusDatos), .Lri(Lri), .CLK(CLK), .CLEAR(in_1), .CO(CO));
  FLAGS flags_1 (.SalidaFlags(alu_1_salidaflags), .Lf(Lf), .CLK(CLK), .CLEAR(in_1), .FLGS(FLGS));
  BUFFERALU bufferalu_1 (.SalidaALU(SalidaALU), .SalAlu(SalAlu), .SalidaBufferALU(BusDatos));

  // Other names for the same wires on the sheet: CLEAR = in_1; datos[7:0] = BusDatos; entDat[7:0] = BusDatos;
  //   RST = in_2
endmodule

module PC (
  input  Lpc,
  input  [15:0] entradaPC,
  input  Ipc,
  input  CLK,
  input  CLEAR,
  output [15:0] salida
);

  Counter #(.max('hffff), .width(16)) counter_1 (
    .load(Lpc), .D(entradaPC), .count(Ipc), .Q(salida), .up(1'b1), .clk(CLK), .clr(CLEAR));  // open: carry
endmodule

module HL (
  input  LL,
  input  LH,
  input  [7:0] BusDatos,
  input  CLK,
  input  CLEAR,
  output [15:0] SalidaHL
);

  Register register_1 (.D(BusDatos), .en(LL), .Q(SalidaHL[7:0]), .clk(CLK), .clr(CLEAR));
  Register register_2 (.D(BusDatos), .en(LH), .Q(SalidaHL[15:8]), .clk(CLK), .clr(CLEAR));
endmodule

module MUXPCHL (
  input  [15:0] SalidaPC,
  input  [15:0] SalidaHL,
  input  SelDir,
  output [15:0] dir,
  output [7:0] dirL,
  output [7:0] dirH
);

  Multiplexer #(.width(16)) multiplexer_1 (.in0(SalidaPC), .in1(SalidaHL), .out(dir), .sel(SelDir));

  assign dirH = dir[15:8];
  assign dirL = dir[7:0];
endmodule

module RI (
  input  [7:0] BusDatos,
  input  Lri,
  input  CLK,
  input  CLEAR,
  output [7:0] CO
);

  Register register_1 (.D(BusDatos), .en(Lri), .Q(CO), .clk(CLK), .clr(CLEAR));
endmodule

module BR (
  input  [7:0] entDat,
  input  [2:0] SelRegRA,
  input  wr,
  input  [2:0] SelRegW,
  input  [2:0] SelRegRB,
  input  CLK,
  input  CLEAR,
  output [7:0] SalA,
  output [7:0] SalB
);

  wire demultiplexer_1_out0, demultiplexer_1_out1, demultiplexer_1_out2, demultiplexer_1_out3,
       demultiplexer_1_out4, demultiplexer_1_out5, demultiplexer_1_out6, demultiplexer_1_out7;
  wire [7:0] register_1_q, register_2_q, register_3_q, register_4_q, register_5_q, register_6_q,
       register_7_q, register_8_q;

  Demultiplexer #(.select(3)) demultiplexer_1 (
    .out0(demultiplexer_1_out0), .out1(demultiplexer_1_out1), .out2(demultiplexer_1_out2),
    .out3(demultiplexer_1_out3), .out4(demultiplexer_1_out4), .out5(demultiplexer_1_out5),
    .out6(demultiplexer_1_out6), .out7(demultiplexer_1_out7), .in(wr), .sel(SelRegW));
  Register register_1 (.D(entDat), .en(demultiplexer_1_out0), .Q(register_1_q), .clk(CLK), .clr(CLEAR));
  Register register_2 (.D(entDat), .en(demultiplexer_1_out1), .Q(register_2_q), .clk(CLK), .clr(CLEAR));
  Register register_3 (.D(entDat), .en(demultiplexer_1_out2), .Q(register_3_q), .clk(CLK), .clr(CLEAR));
  Register register_4 (.D(entDat), .en(demultiplexer_1_out3), .Q(register_4_q), .clk(CLK), .clr(CLEAR));
  Register register_5 (.D(entDat), .en(demultiplexer_1_out4), .Q(register_5_q), .clk(CLK), .clr(CLEAR));
  Register register_6 (.D(entDat), .en(demultiplexer_1_out5), .Q(register_6_q), .clk(CLK), .clr(CLEAR));
  Register register_7 (.D(entDat), .en(demultiplexer_1_out6), .Q(register_7_q), .clk(CLK), .clr(CLEAR));
  Register register_8 (.D(entDat), .en(demultiplexer_1_out7), .Q(register_8_q), .clk(CLK), .clr(CLEAR));
  Multiplexer #(.select(3), .width(8)) multiplexer_1 (
    .in0(register_1_q), .in1(register_2_q), .in2(register_3_q), .in3(register_4_q), .in4(register_5_q),
    .in5(register_6_q), .in6(register_7_q), .in7(register_8_q), .out(SalA), .sel(SelRegRA));
  Multiplexer #(.select(3), .width(8)) multiplexer_2 (
    .in0(register_1_q), .in1(register_2_q), .in2(register_3_q), .in3(register_4_q), .in4(register_5_q),
    .in5(register_6_q), .in6(register_7_q), .in7(register_8_q), .out(SalB), .sel(SelRegRB));
endmodule

module ALU (
  input  [7:0] SalA,
  input  [7:0] SalB,
  input  [2:0] ope,
  output [7:0] SalidaALU,
  output [7:0] SalidaFlags
);

  wire adder_1_cout, adder_2_cout, subtractor_1_bout, subtractor_2_bout;
  wire [7:0] adder_1_out, adder_2_out, and_1_out, not_1_out, subtractor_1_out, subtractor_2_out;

  assign and_1_out = SalA & SalB;  // AND_Gate and_1, 8 bits wide
  assign not_1_out = ~SalA;  // NOT_Gate not_1, 8 bits wide
  Subtractor subtractor_1 (.a(SalA), .b(8'h1), .out(subtractor_1_out), .bin(1'b0), .bout(subtractor_1_bout));
  Adder adder_1 (.a(SalA), .b(SalB), .out(adder_1_out), .cin(1'b0), .cout(adder_1_cout));
  Subtractor subtractor_2 (.a(SalA), .b(SalB), .out(subtractor_2_out), .bin(1'b0), .bout(subtractor_2_bout));
  Adder adder_2 (.a(SalA), .b(8'h1), .out(adder_2_out), .cin(1'b0), .cout(adder_2_cout));
  Multiplexer #(.select(3), .width(8)) multiplexer_1 (
    .in0(SalA), .in1(SalB), .in2(and_1_out), .in3(not_1_out), .in4(subtractor_1_out), .in5(adder_1_out),
    .in6(subtractor_2_out), .in7(adder_2_out), .out(SalidaALU), .sel(ope));
  Multiplexer #(.select(3)) multiplexer_2 (
    .in0(1'b0), .in1(1'b0), .in2(1'b0), .in3(1'b0), .in4(subtractor_1_bout), .in5(adder_1_cout),
    .in6(subtractor_2_bout), .in7(adder_2_cout), .out(SalidaFlags[1]), .sel(ope));
  Comparator comparator_1 (.a(SalidaALU), .b({8{1'b0}}), .eq(SalidaFlags[0]));  // open: gt, lt

  assign SalidaFlags[7:2] = {{5{1'b0}}, SalidaALU[7]};

  // Notes on the sheet:
  //   FS
  //   FC
  //   FZ
endmodule

module FLAGS (
  input  [7:0] SalidaFlags,
  input  Lf,
  input  CLK,
  input  CLEAR,
  output [7:0] FLGS
);

  Register register_1 (.D(SalidaFlags), .en(Lf), .clk(CLK), .Q(FLGS), .clr(CLEAR));
endmodule

module MEMORIA (
  input  [7:0] dirL,
  input  we,
  input  oe,
  input  CLK,
  output [7:0] datos
);

  RAM #(.asyncread("true"), .databus("bidir")) ram_1 (.addr(dirL), .we(we), .oe(oe), .clk(CLK), .data(datos));
endmodule

module BUFFERALU (
  input  [7:0] SalidaALU,
  input  SalAlu,
  output [7:0] SalidaBufferALU
);

  assign SalidaBufferALU = SalAlu ? SalidaALU : 8'bz;  // Controlled_Buffer controlled_buffer_1
endmodule

// VHDL entity unidad_control, as the project stores it:
-- ══════════════════════════════════════════════════════════════════
-- Problema:
-- Se requiere integrar las banderas de estado provenientes del modulo 
-- FLAGS (unificadas en un solo bus de 8 bits llamado FLGS) dentro del 
-- codigo VHDL de la Unidad de Control. 
--
-- Fundamentos Teóricos:
-- 1. Bus Unificado: En lugar de recibir pines individuales para Zero 
--    (FZ), Signo (FS) y Acarreo (FC), la FSM ahora lee un vector de 
--    8 bits, lo cual coincide con la arquitectura esquematica fisica.
-- 2. Alias: En VHDL, se pueden declarar "alias" para darle un nombre 
--    significativo a un bit o segmento especifico de un vector. Esto 
--    evita modificar toda la logica de control condicional existente 
--    (como los saltos), ya que el alias mapea el nombre anterior 
--    al nuevo indice dentro del bus.
--
-- Desglose Paso a Paso:
-- 1. En la entidad `unidad_control`, reemplazar los puertos de entrada
--    `FZ`, `FC` y `FS` por un unico puerto vectorial `FLGS` de 8 bits.
-- 2. En la seccion declarativa de la arquitectura, definir alias 
--    para FZ apuntando a `FLGS(0)`, FC a `FLGS(1)` y FS a `FLGS(2)` 
--    (basado en el diseno del multiplexor/splitter de la ALU).
-- 3. Mantener el bloque de codigo ejecutable identico, ya que los 
--    alias se encargaran de resolver las variables durante la sintesis.
-- ══════════════════════════════════════════════════════════════════

-- ══════════════════════════════════════════════════════════════════
-- Librerias / Dependencias
-- ══════════════════════════════════════════════════════════════════
LIBRARY IEEE;
USE IEEE.STD_LOGIC_1164.ALL;
USE IEEE.NUMERIC_STD.ALL;

-- ══════════════════════════════════════════════════════════════════
-- Entidad / Arquitectura
-- ══════════════════════════════════════════════════════════════════
ENTITY unidad_control IS
    PORT (
        -- Senales globales
        clk       : IN  STD_LOGIC;
        rst       : IN  STD_LOGIC;  -- rst general
        
        -- Entradas de estado desde la Ruta de Datos
        CO        : IN  STD_LOGIC_VECTOR(7 DOWNTO 0); -- Codigo de Operacion (OpCode) desde RI
        
        -- INTEGRACION: Bus unificado de banderas desde el registro FLAGS
        FLGS      : IN  STD_LOGIC_VECTOR(7 DOWNTO 0); 

        -- Salidas de Control hacia la Ruta de Datos
        Lpc       : OUT STD_LOGIC; -- Load PC
        Ipc       : OUT STD_LOGIC; -- Increment PC
        SelDir    : OUT STD_LOGIC; -- Selector del MUX de direcciones
        LH        : OUT STD_LOGIC; -- Load Registro H
        LL        : OUT STD_LOGIC; -- Load Registro L
        Lri       : OUT STD_LOGIC; -- Load Registro de Instruccion
        SelRegW   : OUT STD_LOGIC_VECTOR(2 DOWNTO 0); -- Seleccion Reg Escritura
        wr        : OUT STD_LOGIC; -- Write Enable del Banco de Registros
        SelRegRA  : OUT STD_LOGIC_VECTOR(2 DOWNTO 0); -- Seleccion Reg A
        SelRegRB  : OUT STD_LOGIC_VECTOR(2 DOWNTO 0); -- Seleccion Reg B
        ope       : OUT STD_LOGIC_VECTOR(2 DOWNTO 0); -- Codigo operacion ALU
        SalAlu    : OUT STD_LOGIC; -- Habilita buffer triestado de la ALU
        LF        : OUT STD_LOGIC; -- Load Flags
        
        -- Salidas de Control hacia la Memoria (Adaptado a Logisim de 8 bits)
        oe        : OUT STD_LOGIC; -- Output Enable (Activo Alto - Lectura)
        we        : OUT STD_LOGIC; -- Write Enable (Activo Alto - Escritura)
        
        -- Salida de Estado
        Fin       : OUT STD_LOGIC;  -- Indicador de fin de programa

        -- NUEVO: Salida para visualizar el estado de la FSM en Logisim
        estado_out: OUT STD_LOGIC_VECTOR(4 DOWNTO 0)
    );
END unidad_control;

ARCHITECTURE Behavioral OF unidad_control IS

    -- ══════════════════════════════════════════════════════════════════
    -- Lista de Definiciones y Alias
    -- ══════════════════════════════════════════════════════════════════
    
    -- INTEGRACION: Alias para mapear las banderas al bus FLGS
    ALIAS FZ : STD_LOGIC IS FLGS(0); -- Bandera Zero mapeada al bit 0
    ALIAS FC : STD_LOGIC IS FLGS(1); -- Bandera Carry mapeada al bit 1
    ALIAS FS : STD_LOGIC IS FLGS(2); -- Bandera Sign mapeada al bit 2

    TYPE estado_t IS (
        S00_RESET,
        S01_FETCH0, 
        S02_FETCH1,
        S03_LOAD0_STORE0, 
        S04_LOAD1_STORE1, 
        S05_LOAD2_STORE2, 
        S06_LOAD3_STORE3, 
        S07_LOAD4,
        S08_STORE5,
        S09_ADD0,
        S10_MOV0,
        S11_FIN0,
        S12_MOVI0, 
        S13_MOVI1,
        S14_JMP_COND,
        S15_NOT0,
        S16_AND0,
        S17_DEC0,
        S18_INC0,
        S19_SUB0
    );

    SIGNAL estado_actual, estado_siguiente : estado_t;

BEGIN
    -- Mapeo del estado actual a una salida binaria para Sondas en Logisim
    WITH estado_actual SELECT
        estado_out <= "00000" WHEN S00_RESET,
                      "00001" WHEN S01_FETCH0,
                      "00010" WHEN S02_FETCH1,
                      "00011" WHEN S03_LOAD0_STORE0,
                      "00100" WHEN S04_LOAD1_STORE1,
                      "00101" WHEN S05_LOAD2_STORE2,
                      "00110" WHEN S06_LOAD3_STORE3,
                      "00111" WHEN S07_LOAD4,
                      "01000" WHEN S08_STORE5,
                      "01001" WHEN S09_ADD0,
                      "01010" WHEN S10_MOV0,
                      "01011" WHEN S11_FIN0,
                      "01100" WHEN S12_MOVI0,
                      "01101" WHEN S13_MOVI1,
                      "01110" WHEN S14_JMP_COND,
                      "01111" WHEN S15_NOT0,
                      "10000" WHEN S16_AND0,
                      "10001" WHEN S17_DEC0,
                      "10010" WHEN S18_INC0,
                      "10011" WHEN S19_SUB0,
                      "11111" WHEN OTHERS;

    -- ══════════════════════════════════════════════════════════════════
    -- Codigo Ejecutable / Main
    -- ══════════════════════════════════════════════════════════════════

    -- Proceso Secuencial: Transicion de Estados
    PROCESS(clk, rst)
    BEGIN
        IF rst = '1' THEN
            estado_actual <= S00_RESET;
        ELSIF rising_edge(clk) THEN
            estado_actual <= estado_siguiente;
        END IF;
    END PROCESS;

    -- Proceso Combinacional: Logica de proximo estado y de salidas
    -- INTEGRACION: Eliminamos FZ, FC, FS de la lista sensitiva y agregamos FLGS
    PROCESS(estado_actual, CO, FLGS)
    BEGIN
        -- 1. Valores por defecto (Seguridad)
        -- Apagar todas las senales activas en ALTO
        Lpc <= '0'; 
        Ipc <= '0'; 
        SelDir <= '0';
        LH <= '0'; 
        LL <= '0'; 
        Lri <= '0'; 
        wr <= '0';
        SalAlu <= '0'; 
        LF <= '0'; 
        Fin <= '0';
        
        -- Senales de Memoria (Adaptadas al circuito MUXPCHL)
        oe <= '0'; 
        we <= '0'; 
        
        -- Buses de control
        SelRegW <= "000"; 
        SelRegRA <= "000"; 
        SelRegRB <= "000"; 
        ope <= "000";
        
        estado_siguiente <= estado_actual; -- Por defecto, retener estado

        -- 2. Decodificacion de Maquina de Estados
        CASE estado_actual IS
        
            WHEN S00_RESET =>
                estado_siguiente <= S01_FETCH0;

            WHEN S01_FETCH0 =>
                oe <= '1'; -- Activamos lectura de memoria
                Lri  <= '1'; -- Cargamos instruccion
                estado_siguiente <= S02_FETCH1;

            WHEN S02_FETCH1 =>
                Ipc <= '1';
                -- === DECODIFICADOR CENTRAL ===
                CASE CO IS
                    WHEN x"40" => estado_siguiente <= S15_NOT0;
                    WHEN x"41" => estado_siguiente <= S16_AND0;
                    WHEN x"42" => estado_siguiente <= S17_DEC0;
                    WHEN x"43" => estado_siguiente <= S18_INC0;
                    WHEN x"44" => estado_siguiente <= S19_SUB0;
                    WHEN x"45" => estado_siguiente <= S09_ADD0;
                    WHEN x"46" => estado_siguiente <= S10_MOV0;
                    WHEN x"47" => estado_siguiente <= S12_MOVI0;
                    
                    WHEN x"70" => estado_siguiente <= S03_LOAD0_STORE0;
                    WHEN x"71" => estado_siguiente <= S03_LOAD0_STORE0;

                    WHEN x"80" => estado_siguiente <= S03_LOAD0_STORE0;
                    WHEN x"81" => estado_siguiente <= S03_LOAD0_STORE0;
                    WHEN x"82" => estado_siguiente <= S03_LOAD0_STORE0;
                    WHEN x"83" => estado_siguiente <= S03_LOAD0_STORE0;
                    
                    WHEN x"FF" => estado_siguiente <= S11_FIN0;
                    WHEN OTHERS => estado_siguiente <= S01_FETCH0;
                END CASE;

            -- === ESTADOS COMUNES ===
            WHEN S03_LOAD0_STORE0 =>
                oe <= '1'; 
                LL <= '1';
                estado_siguiente <= S04_LOAD1_STORE1;
                
            WHEN S04_LOAD1_STORE1 =>
                Ipc <= '1';
                estado_siguiente <= S05_LOAD2_STORE2;
                
            WHEN S05_LOAD2_STORE2 =>
                oe <= '1'; 
                LH <= '1';
                estado_siguiente <= S06_LOAD3_STORE3;
                
		  WHEN S06_LOAD3_STORE3 =>
                Ipc <= '1';
                IF CO = x"70" THEN
                    estado_siguiente <= S07_LOAD4;
                ELSIF CO = x"71" THEN
                    estado_siguiente <= S08_STORE5;
                ELSIF CO = x"80" THEN
                    estado_siguiente <= S14_JMP_COND;
                ELSIF CO = x"81" THEN
                    IF FZ = '1' THEN estado_siguiente <= S14_JMP_COND;
                    ELSE estado_siguiente <= S01_FETCH0;
                    END IF;
                ELSIF CO = x"82" THEN
                    IF FC = '1' THEN estado_siguiente <= S14_JMP_COND;
                    ELSE estado_siguiente <= S01_FETCH0;
                    END IF;
                ELSIF CO = x"83" THEN
                    IF FS = '1' THEN estado_siguiente <= S14_JMP_COND;
                    ELSE estado_siguiente <= S01_FETCH0;
                    END IF;
                ELSE
                    estado_siguiente <= S01_FETCH0;
                END IF;

            -- === EJECUCION DE ACCESO A MEMORIA ===
            
            -- LOAD (70h)
            WHEN S07_LOAD4 =>
                SelDir <= '1'; -- MUX envia dirL a la memoria
                oe <= '1';     -- Leemos de la direccion dirL
                SelRegW <= "001";
                wr <= '1';
                estado_siguiente <= S01_FETCH0;
                
            -- STORE (71h)
            WHEN S08_STORE5 =>
                SelDir <= '1'; -- MUX envia dirL a la memoria
                we <= '1';     -- Habilitamos escritura (Write Enable)
                SelRegRA <= "001";
                ope <= "000";
                SalAlu <= '1'; -- El dato de R1 fluye al BusDatos
                estado_siguiente <= S01_FETCH0;
                
            -- ADD (45h)
            WHEN S09_ADD0 =>
                SelRegRA <= "000"; 
                SelRegRB <= "001"; 
                SelRegW <= "001";
                ope <= "101"; 
                SalAlu <= '1'; 
                LF <= '1'; 
                wr <= '1';
                estado_siguiente <= S01_FETCH0;
                
            -- MOV (46h)
            WHEN S10_MOV0 =>
                SelRegRA <= "001"; 
                SelRegW <= "000"; 
                ope <= "000";
                SalAlu <= '1'; 
                wr <= '1';
                estado_siguiente <= S01_FETCH0;
                
            -- FIN (FFh)
            WHEN S11_FIN0 =>
                Fin <= '1';
                estado_siguiente <= S11_FIN0;
                
            -- MOVI (47h)
            WHEN S12_MOVI0 =>
                oe <= '1'; 
                SelRegW <= "001"; 
                wr <= '1';
                estado_siguiente <= S13_MOVI1;
                
            WHEN S13_MOVI1 =>
                Ipc <= '1';
                estado_siguiente <= S01_FETCH0;

            -- SALTOS
            -- INTEGRACION: Las variables FZ, FC y FS utilizadas aqui ahora
            -- hacen referencia a los bits especificos de FLGS gracias a los ALIAS.
            -- CORRECCION: Ejecucion incondicional del salto con SelDir activado
            WHEN S14_JMP_COND =>
                SelDir <= '1'; -- REDIRIGE EL MUX HACIA EL REGISTRO HL
                Lpc <= '1';    -- CARGA EL PC
                estado_siguiente <= S01_FETCH0;

            -- ALU (Resto de operaciones)
            WHEN S15_NOT0 =>
                SelRegRA <= "001"; 
                SelRegW <= "001";
                ope <= "011"; 
                SalAlu <= '1'; 
                LF <= '1'; 
                wr <= '1';
                estado_siguiente <= S01_FETCH0;
                
            WHEN S16_AND0 =>
                SelRegRA <= "000"; 
                SelRegRB <= "001"; 
                SelRegW <= "001";
                ope <= "010"; 
                SalAlu <= '1'; 
                LF <= '1'; 
                wr <= '1';
                estado_siguiente <= S01_FETCH0;
                
            WHEN S17_DEC0 =>
                SelRegRA <= "001"; 
                SelRegW <= "001";
                ope <= "100"; 
                SalAlu <= '1'; 
                LF <= '1'; 
                wr <= '1';
                estado_siguiente <= S01_FETCH0;
                
            WHEN S18_INC0 =>
                SelRegRA <= "001"; 
                SelRegW <= "001";
                ope <= "111"; 
                SalAlu <= '1'; 
                LF <= '1'; 
                wr <= '1';
                estado_siguiente <= S01_FETCH0;
                
            WHEN S19_SUB0 =>
                SelRegRA <= "000"; 
                SelRegRB <= "001"; 
                SelRegW <= "001";
                ope <= "110"; 
                SalAlu <= '1'; 
                LF <= '1'; 
                wr <= '1';
                estado_siguiente <= S01_FETCH0;

            WHEN OTHERS =>
                estado_siguiente <= S01_FETCH0;
                
        END CASE;
    END PROCESS;
END Behavioral;
